// Digital circuit 2bit-comparator.dig as structural Verilog
module _2bit_comparator (
  input  B,
  input  A,
  output out_1,
  output out_2,
  output out_3
);

  wire nand_1_out, nand_2_out;

  nand nand_1 (nand_1_out, A, A);
  nand nand_2 (nand_2_out, B, B);
  nand nand_3 (out_1, nand_1_out, B);
  nand nand_4 (out_2, A, nand_2_out);
  nand nand_5 (out_3, out_1, out_2);
endmodule
