// Digital circuit JK-flip-flop.dig as structural Verilog
module JK_flip_flop (
  input  in_3,
  input  in_4,
  input  in_5,
  output out_1,
  output out_2
);

  wire nand_1_out, nand_2_out, nand_3_out, nand_4_out, nand_5_out, nand_6_out;

  nand nand_1 (nand_1_out, in_3, out_2);
  nand nand_2 (nand_2_out, out_1, in_4);
  nand nand_3 (nand_3_out, nand_1_out, nand_1_out);
  nand nand_4 (nand_4_out, nand_2_out, nand_2_out);
  nand nand_5 (nand_5_out, nand_3_out, in_5);
  nand nand_6 (nand_6_out, nand_4_out, in_5);
  nand nand_7 (out_1, nand_5_out, out_2);
  nand nand_8 (out_2, out_1, nand_6_out);
endmodule
