// Digital circuit binary counter.dig as structural Verilog
module binary_counter (
  input  in_1,
  input  in_6,
  output out_2,
  output out_3,
  output out_4,
  output out_5
);

  wire and_1_out, d_ff_1_nq, d_ff_2_nq, d_ff_3_nq, d_ff_4_nq;

  D_FF d_ff_1 (.D(and_1_out), .C(in_1), .Q(out_2), .nQ(d_ff_1_nq));
  and and_1 (and_1_out, d_ff_1_nq, in_6);
  D_FF d_ff_2 (.D(d_ff_2_nq), .C(out_2), .Q(out_3), .nQ(d_ff_2_nq));
  D_FF d_ff_3 (.D(d_ff_3_nq), .C(out_3), .Q(out_4), .nQ(d_ff_3_nq));
  D_FF d_ff_4 (.D(d_ff_4_nq), .C(out_4), .Q(out_5), .nQ(d_ff_4_nq));
endmodule
