// Digital circuit counter-binary-uu.dig as structural Verilog
module counter_binary_uu (
  input  in_4,
  input  in_5,
  input  in_9,
  input  in_10,
  output out_1,
  output out_2,
  output out_3,
  output out_6,
  output out_7,
  output out_8
);

  wire jk_ff_1_nq, jk_ff_2_q, jk_ff_3_nq, jk_ff_4_q;

  JK_FF jk_ff_1 (.J(in_5), .C(in_4), .K(in_5), .Q(out_1), .nQ(jk_ff_1_nq));
  JK_FF jk_ff_2 (.J(in_10), .C(in_9), .K(in_10), .Q(jk_ff_2_q), .nQ(out_6));
  JK_FF jk_ff_3 (.J(in_5), .C(jk_ff_1_nq), .K(in_5), .Q(out_2), .nQ(jk_ff_3_nq));
  JK_FF jk_ff_4 (.J(in_10), .C(jk_ff_2_q), .K(in_10), .Q(jk_ff_4_q), .nQ(out_7));
  JK_FF jk_ff_5 (.J(in_5), .C(jk_ff_3_nq), .K(in_5), .Q(out_3));  // open: nQ
  JK_FF jk_ff_6 (.J(in_10), .C(jk_ff_4_q), .K(in_10), .Q(out_8));  // open: nQ
endmodule
