// Digital circuit jelly one.dig as structural Verilog
module jelly_one (
  input  clk
);

  wire _28c16_1_p9, _28c16_1_p10, _28c16_1_p11, _28c16_1_p13, _28c16_1_p14, _28c16_1_p15, _28c16_1_p16,
       _28c16_1_p17, _28c16_1_p18, _7474_1_p1, _74193_1_pin2, _74193_1_pin3, _74193_1_pin6, _74193_1_pin7,
       _74193_1_pin8, _74574_1_pin2, _74574_1_pin3, _74574_1_pin4, _74574_1_pin5, _74574_1_pin6,
       _74574_1_pin7, _74574_1_pin8, _74574_1_pin9, _74574_1_pin11, _74574_1_pin12, _74574_1_pin13,
       _74574_1_pin14, _74574_1_pin15, _74574_1_pin16, _74574_1_pin17, _74574_1_pin18, _74574_1_pin19;

  _74574 _74574_1 (
    .pin2(_74574_1_pin2), .pin3(_74574_1_pin3), .pin4(_74574_1_pin4), .pin5(_74574_1_pin5),
    .pin6(_74574_1_pin6), .pin7(_74574_1_pin7), .pin8(_74574_1_pin8), .pin9(_74574_1_pin9),
    .pin11(_74574_1_pin11), .pin12(_74574_1_pin12), .pin13(_74574_1_pin13), .pin14(_74574_1_pin14),
    .pin15(_74574_1_pin15), .pin16(_74574_1_pin16), .pin17(_74574_1_pin17), .pin18(_74574_1_pin18),
    .pin19(_74574_1_pin19));  // open: pin1, pin10, pin20
  // _74574 _74574_2: pin names not known
  // _74574 _74574_3: pin names not known
  _74193 _74193_1 (
    .pin2(_74193_1_pin2), .pin3(_74193_1_pin3), .pin5(clk), .pin6(_74193_1_pin6), .pin7(_74193_1_pin7),
    .pin8(_74193_1_pin8));  // open: pin1, pin4, pin9, pin10, pin11, pin12, pin13, pin14, pin15, pin16
  // _28c16 _28c16_1: pin names not known; wires that end beside it: _74574_1_pin19, _74574_1_pin18, _74574_1_pin17, _74574_1_pin16, _74193_1_pin7, _74193_1_pin6, _74193_1_pin2, _74193_1_pin3, _28c16_1_p9, _28c16_1_p10, _28c16_1_p11, _74193_1_pin8, _28c16_1_p13, _28c16_1_p14, _28c16_1_p15, _28c16_1_p16, _28c16_1_p17, _28c16_1_p18, _28c16_1_p13, _28c16_1_p14
  // _7474 _7474_1: pin names not known; wires that end beside it: _7474_1_p1, _7474_1_p1
endmodule
