// Digital circuit jelly-7-glue-minimal.dig as structural Verilog
module jelly_7_glue_minimal (
  input  D0,
  input  D1,
  input  D2,
  input  D3,
  input  D4,
  input  D5,
  input  D6,
  input  D7,
  input  mode__U3_Q4,
  input  T1__U3_D1,
  input  T0__U3_D0,
  input  move__U3_Q5,
  input  mode__U3_Q5,
  input  move__U3_Q6,
  input  clear__U3_Q7,
  output U1_A8___U3_A8,
  output Connector__eq_T0_eq,
  output move,
  output U1_A7___U3_A7,
  output U1_A8___U3_A9,
  output U1_A9___U3_A10
);

  wire and_1_out, d_ff_1_nq, d_ff_2_nq;

  PullDown pulldown_1 (.out(D0));
  PullDown pulldown_2 (.out(D1));
  D_FF d_ff_1 (.D(d_ff_1_nq), .C(mode__U3_Q4), .Q(U1_A8___U3_A8), .nQ(d_ff_1_nq));
  D_FF d_ff_2 (.D(d_ff_2_nq), .C(move__U3_Q5), .Q(move), .nQ(d_ff_2_nq));
  PullDown pulldown_3 (.out(D2));
  PullDown pulldown_4 (.out(D3));
  LED led_1 (.in(clear__U3_Q7));
  PullDown pulldown_5 (.out(D4));
  PullDown pulldown_6 (.out(D5));
  PullDown pulldown_7 (.out(D6));
  PullDown pulldown_8 (.out(D7));
  LED led_2 (.in(U1_A8___U3_A8));
  LED led_3 (.in(move));
  and and_1 (and_1_out, move, T1__U3_D1);
  // PolarityAwareLED polarityawareled_1: pin names not known; wires that end beside it: D0, U1_A7___U3_A7
  // PolarityAwareLED polarityawareled_2: pin names not known; wires that end beside it: D1, U1_A7___U3_A7
  // PolarityAwareLED polarityawareled_3: pin names not known; wires that end beside it: D2, U1_A7___U3_A7
  // PolarityAwareLED polarityawareled_4: pin names not known; wires that end beside it: D3, U1_A7___U3_A7
  // PolarityAwareLED polarityawareled_5: pin names not known; wires that end beside it: D4, U1_A7___U3_A7
  // PolarityAwareLED polarityawareled_6: pin names not known; wires that end beside it: D5, U1_A7___U3_A7
  // PolarityAwareLED polarityawareled_7: pin names not known; wires that end beside it: D6, U1_A7___U3_A7
  // PolarityAwareLED polarityawareled_8: pin names not known; wires that end beside it: D7, U1_A7___U3_A7
  PullDown pulldown_9 (.out(U1_A7___U3_A7));
  xor xor_1 (Connector__eq_T0_eq, and_1_out, T0__U3_D0);
  LED led_4 (.in(U1_A7___U3_A7));
  LED led_5 (.in(mode__U3_Q5));
  LED led_6 (.in(move__U3_Q6));

  assign U1_A8___U3_A9 = mode__U3_Q5;
  assign U1_A9___U3_A10 = move__U3_Q6;

  // Notes on the sheet:
  //   Using Chips
  //   PS. 74HC74 have a clear
  //   Zero Detector
  //   Not Using Chips
endmodule
