// Digital circuit jelly-glue-less.logic.dig as structural Verilog
module jelly_glue_less_logic (
  input  D0,
  input  D1,
  input  D2,
  input  D3,
  input  D4,
  input  D5,
  input  D6,
  input  D7,
  input  U3__while,
  input  U3__again,
  input  mode,
  input  U3_T1,
  input  U3_T0,
  input  move_2,
  input  zero,
  output mode_2,
  output Connector__eq_T0_eq,
  output move,
  output zero_2
);

  wire and_1_out, and_2_out, and_3_out, and_4_out, and_5_out, and_6_out, d_ff_1_nq, d_ff_2_nq, nand_1_out,
       nand_2_out, or_1_out, or_2_out, or_3_out;

  nand nand_1 (nand_1_out, zero, zero);
  PullDown pulldown_1 (.out(D0));
  PullDown pulldown_2 (.out(D1));
  PullDown pulldown_3 (.out(D2));
  PullDown pulldown_4 (.out(D3));
  and and_1 (and_1_out, U3__again, zero);
  and and_2 (and_2_out, U3__while, nand_1_out);
  and and_3 (and_3_out, move_2, U3_T1);
  PullDown pulldown_5 (.out(D4));
  PullDown pulldown_6 (.out(D5));
  PullDown pulldown_7 (.out(D6));
  PullDown pulldown_8 (.out(D7));
  or or_1 (or_1_out, and_1_out, and_2_out);
  nand nand_2 (nand_2_out, mode, mode);
  and and_4 (and_4_out, nand_1_out, mode);
  xor xor_1 (Connector__eq_T0_eq, and_3_out, U3_T0);
  // PolarityAwareLED polarityawareled_1: pin names not known; wires that end beside it: D0, zero_2
  // PolarityAwareLED polarityawareled_2: pin names not known; wires that end beside it: D1, zero_2
  // PolarityAwareLED polarityawareled_3: pin names not known; wires that end beside it: D2, zero_2
  // PolarityAwareLED polarityawareled_4: pin names not known; wires that end beside it: D3, zero_2
  // PolarityAwareLED polarityawareled_5: pin names not known; wires that end beside it: D4, zero_2
  // PolarityAwareLED polarityawareled_6: pin names not known; wires that end beside it: D5, zero_2
  // PolarityAwareLED polarityawareled_7: pin names not known; wires that end beside it: D6, zero_2
  // PolarityAwareLED polarityawareled_8: pin names not known; wires that end beside it: D7, zero_2
  PullDown pulldown_9 (.out(zero_2));
  and and_5 (and_5_out, or_1_out, nand_2_out);
  or or_2 (or_2_out, and_5_out, and_4_out);
  and and_6 (and_6_out, and_4_out, move_2);
  or or_3 (or_3_out, and_1_out, and_6_out);
  D_FF d_ff_1 (.D(d_ff_1_nq), .C(or_2_out), .Q(mode_2), .nQ(d_ff_1_nq));
  D_FF d_ff_2 (.D(d_ff_2_nq), .C(or_3_out), .Q(move), .nQ(d_ff_2_nq));

  // Notes on the sheet:
  //   Zero Detector
endmodule
