// Digital circuit jelly-glue-loop.dig as structural Verilog
module jelly_glue_loop (
  input  \begin ,
  input  again,
  input  zero,
  output out_3,
  output out_4,
  output out_6,
  output out_7,
  output S9,
  output S10,
  output S9_2,
  output S10_2,
  output toggle9,
  output toggle10
);

  wire and_2_out, and_3_out, and_4_out, d_ff_1_nq, d_ff_2_nq, or_1_out, or_2_out;

  nor nor_1 (out_3, toggle9, toggle10);
  nor nor_2 (out_4, \begin , again);
  nor nor_3 (out_6, again, zero);
  and and_1 (out_7, again, zero);
  and and_2 (and_2_out, out_6, out_4);
  and and_3 (and_3_out, out_6, out_3);
  and and_4 (and_4_out, out_7, out_3);
  and and_5 (S9, toggle9, and_2_out);
  and and_6 (S10, toggle10, and_2_out);
  and and_7 (S9_2, \begin , and_3_out);
  and and_8 (S10_2, again, and_4_out);
  LED led_1 (.in(S10));
  LED led_2 (.in(S9));
  LED led_3 (.in(S9_2));
  LED led_4 (.in(S10_2));
  or or_1 (or_1_out, S9, S9_2);
  or or_2 (or_2_out, S10, S10_2);
  LED led_5 (.in(toggle9));
  LED led_6 (.in(toggle10));
  D_FF d_ff_1 (.D(d_ff_1_nq), .C(or_1_out), .Q(toggle9), .nQ(d_ff_1_nq));
  D_FF d_ff_2 (.D(d_ff_2_nq), .C(or_2_out), .Q(toggle10), .nQ(d_ff_2_nq));
endmodule
