// Digital circuit jelly-glues-ttls.dig as structural Verilog
module jelly_glues_ttls (
  input  \begin ,
  input  again,
  input  A9,
  input  A10,
  input  in_5,
  input  in_6,
  input  in_11,
  output out_7,
  output out_8,
  output out_9,
  output out_10
);

  wire _7400_1_pin3, _7400_1_pin6, _7400_1_pin9, _7400_2_pin3, _7400_2_pin6, _7400_2_pin9, _7400_3_pin3,
       _7400_3_pin9, _7400_4_pin3, _7400_4_pin6, _7400_4_pin8, _7400_4_pin9, _7400_4_pin11, _7400_5_pin3,
       _7400_5_pin6;

  _7400 _7400_1 (
    .pin1(A9), .pin2(A9), .pin3(_7400_1_pin3), .pin4(A10), .pin5(A10), .pin6(_7400_1_pin6), .pin7(1'b0),
    .pin8(out_8), .pin9(_7400_1_pin9), .pin10(_7400_1_pin9), .pin11(_7400_1_pin9), .pin12(_7400_1_pin6),
    .pin13(_7400_1_pin3), .pin14(1'b1));
  _7400 _7400_2 (
    .pin1(\begin ), .pin2(\begin ), .pin3(_7400_2_pin3), .pin4(again), .pin5(again), .pin6(_7400_2_pin6),
    .pin7(1'b0), .pin8(out_9), .pin9(_7400_2_pin9), .pin10(_7400_2_pin9), .pin11(_7400_2_pin9),
    .pin12(_7400_2_pin6), .pin13(_7400_2_pin3), .pin14(1'b1));
  _7400 _7400_3 (
    .pin1(in_11), .pin2(in_11), .pin3(_7400_3_pin3), .pin4(1'b0), .pin5(1'b0), .pin7(1'b0), .pin8(out_10),
    .pin9(_7400_3_pin9), .pin10(_7400_3_pin9), .pin11(_7400_3_pin9), .pin12(_7400_2_pin6),
    .pin13(_7400_3_pin3), .pin14(1'b1));  // open: pin6
  _7400 _7400_4 (
    .pin1(in_5), .pin2(in_5), .pin3(_7400_4_pin3), .pin4(in_6), .pin5(in_6), .pin6(_7400_4_pin6),
    .pin7(1'b0), .pin8(_7400_4_pin8), .pin9(_7400_4_pin9), .pin10(_7400_4_pin9), .pin11(_7400_4_pin11),
    .pin12(_7400_4_pin6), .pin13(_7400_4_pin3), .pin14(1'b1));
  _7400 _7400_5 (
    .pin1(_7400_4_pin9), .pin2(_7400_4_pin11), .pin3(_7400_5_pin3), .pin4(_7400_4_pin11),
    .pin5(_7400_4_pin8), .pin6(_7400_5_pin6), .pin7(1'b0), .pin8(_7400_4_pin9), .pin9(out_7),
    .pin10(_7400_5_pin6), .pin11(out_7), .pin12(_7400_4_pin9), .pin13(_7400_5_pin3), .pin14(1'b1));
endmodule
