// Digital circuit jelly-glues.x.dig as structural Verilog
module jelly_glues_x (
  input  T0,
  input  T1,
  input  M3,
  input  M2,
  input  M1,
  input  M0,
  input  T2,
  input  T3,
  output OE6,
  output OE7,
  output CS5,
  output CS4,
  output A10,
  output A9,
  output A8,
  output CS6,
  output next,
  output again,
  output \begin ,
  output CLR3,
  output OE6_2,
  output OE7_2
);

  wire and_7_out, and_8_out, and_9_out, and_10_out, and_11_out, and_12_out, and_13_out, and_14_out,
       nand_1_out, nand_4_out, nand_5_out, nand_6_out, nand_7_out, nand_8_out, undriven, undriven_2;

  and and_1 (A10, M3, M2);
  and and_2 (A9, M3, M1);
  and and_3 (A8, M3, M0);
  nand nand_1 (nand_1_out, M3, M3);
  nand nand_2 (OE6, undriven, undriven);
  nand nand_3 (OE7, undriven_2, undriven_2);
  and and_4 (next, nand_1_out, M2);
  and and_5 (again, nand_1_out, M1);
  and and_6 (\begin , nand_1_out, M0);
  nand nand_4 (nand_4_out, T0, T0);
  nand nand_5 (nand_5_out, T1, T1);
  nand nand_6 (nand_6_out, T2, T2);
  nand nand_7 (nand_7_out, T3, T3);
  and and_7 (and_7_out, T0, T1);
  and and_8 (and_8_out, T0, nand_5_out);
  and and_9 (and_9_out, nand_4_out, T1);
  and and_10 (and_10_out, nand_4_out, nand_5_out);
  and and_11 (and_11_out, T2, T3);
  and and_12 (and_12_out, T2, nand_7_out);
  and and_13 (and_13_out, nand_6_out, T3);
  and and_14 (and_14_out, nand_6_out, nand_7_out);
  nand nand_8 (nand_8_out, and_7_out, and_7_out);
  and and_15 (OE6_2, nand_8_out, and_11_out);
  and and_16 (OE7_2, nand_8_out, and_13_out);

  assign CS6 = M3;

  // Notes on the sheet:
  //   5, 6, 7
  //   8, 9, 10
  //   t0=0, t1=0
  //   t0=0, t1=1
  //   t0=1, t1=0
  //   t0=1, t1=1
  //   t2=0, t3=0
  //   t2=0, t3=1
  //   t2=1, t3=0
  //   t2=1, t3=1
endmodule
