// Digital circuit jelly-page-logic-v1.dig as structural Verilog
module jelly_page_logic_v1 (
  input  A_page,
  input  B_back,
  input  C_zero,
  input  D_begin,
  input  E_again,
  output F1,
  output G1,
  output F2,
  output G2,
  output out_10,
  output out_11
);

  wire and_2_out, and_3_out, and_5_out, and_6_out, d_ff_1_nq, d_ff_2_nq, not_1_out, not_2_out, or_2_out,
       or_3_out;

  not not_1 (not_1_out, out_10);
  not not_2 (not_2_out, C_zero);
  and and_1 (F2, out_10, not_2_out);
  and and_2 (and_2_out, not_1_out, not_2_out);
  and and_3 (and_3_out, not_1_out, C_zero);
  and and_4 (G2, F2, out_11);
  and and_5 (and_5_out, and_2_out, D_begin);
  and and_6 (and_6_out, and_3_out, E_again);
  or or_1 (F1, and_5_out, and_6_out);
  and and_7 (G1, F1, C_zero);
  or or_2 (or_2_out, F2, F1);
  or or_3 (or_3_out, G2, G1);
  D_FF d_ff_1 (.D(d_ff_1_nq), .C(or_2_out), .Q(out_10), .nQ(d_ff_1_nq));
  D_FF d_ff_2 (.D(d_ff_2_nq), .C(or_3_out), .Q(out_11), .nQ(d_ff_2_nq));
endmodule
