// Digital circuit jelly-page-logic-v2.dig as structural Verilog
module jelly_page_logic_v2 (
  input  A_page,
  input  B_back,
  input  C_zero,
  input  D_begin,
  input  E_again,
  output F1,
  output G1,
  output F2,
  output G2,
  output out_10,
  output out_11
);

  wire d_ff_1_nq, d_ff_2_nq, nand_1_out, nand_2_out, nand_3_out, nand_4_out, nand_5_out, nand_7_out,
       nand_8_out, nand_9_out, nand_10_out, nand_14_out, nand_15_out, nand_16_out, nand_17_out;

  nand nand_1 (nand_1_out, out_10, out_10);
  nand nand_2 (nand_2_out, C_zero, C_zero);
  nand nand_3 (nand_3_out, out_10, nand_2_out);
  nand nand_4 (nand_4_out, nand_1_out, nand_2_out);
  nand nand_5 (nand_5_out, nand_1_out, C_zero);
  nand nand_6 (F1, nand_3_out, nand_3_out);
  nand nand_7 (nand_7_out, nand_4_out, nand_4_out);
  nand nand_8 (nand_8_out, nand_5_out, nand_5_out);
  nand nand_9 (nand_9_out, nand_7_out, D_begin);
  nand nand_10 (nand_10_out, nand_8_out, E_again);
  nand nand_11 (F2, nand_9_out, nand_10_out);
  nand nand_12 (G1, F1, out_11);
  nand nand_13 (G2, F2, C_zero);
  nand nand_14 (nand_14_out, F1, F1);
  nand nand_15 (nand_15_out, F2, F2);
  nand nand_16 (nand_16_out, nand_14_out, nand_15_out);
  nand nand_17 (nand_17_out, G1, G2);
  D_FF d_ff_1 (.D(d_ff_1_nq), .C(nand_16_out), .Q(out_10), .nQ(d_ff_1_nq));
  D_FF d_ff_2 (.D(d_ff_2_nq), .C(nand_17_out), .Q(out_11), .nQ(d_ff_2_nq));
endmodule
