// Digital circuit jelly-seven-glue.dig as structural Verilog
module jelly_seven_glue (
  input  D0,
  input  D1,
  input  D2,
  input  D3,
  input  D4,
  input  D5,
  input  D6,
  input  D7,
  input  MOVE,
  input  T1,
  input  T0,
  input  T0_2,
  input  T1_2,
  input  T2,
  input  T3,
  input  C0,
  input  C2,
  input  C1,
  input  C3,
  output out_9,
  output out_13,
  output M0,
  output M1,
  output CS6,
  output M2,
  output CS4,
  output CS5,
  output OE7,
  output OE6,
  output move_2,
  output mode,
  output clear,
  output out_33,
  output move_to,
  output mode_to
);

  wire _7400_3_pin3, _7400_3_pin4, _7400_3_pin5, _7408_1_pin3, _7408_1_pin6, _7408_1_pin11, _7408_1_pin12,
       _7408_4_pin1, _7408_4_pin8, _7408_4_pin11, _7408_5_pin3, _7432_1_pin3, _7432_1_pin6, _7432_1_pin8,
       _7432_1_pin11, _7432_2_pin3, _7432_2_pin6, _7474_1_pin1, _7474_1_pin2, _7474_1_pin8;

  _7408 _7408_1 (
    .pin1(T0_2), .pin2(T1_2), .pin3(_7408_1_pin3), .pin4(T2), .pin5(T3), .pin6(_7408_1_pin6), .pin7(1'b0),
    .pin8(out_33), .pin9(_7408_1_pin6), .pin10(_7408_1_pin3), .pin11(_7408_1_pin11), .pin12(_7408_1_pin12),
    .pin13(out_33), .pin14(1'b1));
  _7408 _7408_2 (
    .pin1(out_33), .pin2(C0), .pin3(M0), .pin4(out_33), .pin5(C1), .pin6(M1), .pin7(1'b0), .pin8(M2),
    .pin9(out_33), .pin10(C2), .pin11(CS6), .pin12(out_33), .pin13(C3), .pin14(1'b1));
  _7408 _7408_3 (
    .pin1(_7408_1_pin11), .pin2(C0), .pin3(move_2), .pin4(_7408_1_pin11), .pin5(C1), .pin6(mode),
    .pin7(1'b0), .pin8(clear), .pin9(_7408_1_pin11), .pin10(C2), .pin12(clear), .pin13(clear), .pin14(1'b1));  // open: pin11
  _7408 _7408_4 (
    .pin1(_7408_4_pin1), .pin2(C0), .pin3(CS4), .pin4(_7408_4_pin1), .pin5(C1), .pin6(CS5), .pin7(1'b0),
    .pin8(_7408_4_pin8), .pin9(_7408_4_pin1), .pin10(C2), .pin11(_7408_4_pin11), .pin12(_7408_4_pin1),
    .pin13(C3), .pin14(1'b1));
  _7474 _7474_1 (
    .pin1(_7474_1_pin1), .pin2(_7474_1_pin2), .pin3(move_2), .pin4(1'b1), .pin5(move_to),
    .pin6(_7474_1_pin2), .pin7(1'b0), .pin8(_7474_1_pin8), .pin9(mode_to), .pin10(1'b1), .pin11(mode),
    .pin12(_7474_1_pin8), .pin13(_7474_1_pin1), .pin14(1'b1));
  _7408 _7408_5 (
    .pin1(T1), .pin2(MOVE), .pin3(_7408_5_pin3), .pin4(T1), .pin5(MOVE), .pin7(1'b0), .pin9(1'b1),
    .pin10(1'b1), .pin12(1'b1), .pin13(1'b1), .pin14(1'b1));  // open: pin6, pin8, pin11
  _7400 _7400_1 (
    .pin1(out_33), .pin2(out_33), .pin3(_7408_4_pin1), .pin4(C3), .pin5(C3), .pin6(_7408_1_pin12),
    .pin7(1'b0), .pin8(OE6), .pin9(_7408_4_pin8), .pin10(_7408_4_pin8), .pin11(OE7), .pin12(_7408_4_pin11),
    .pin13(_7408_4_pin11), .pin14(1'b1));
  _7400 _7400_2 (
    .pin1(clear), .pin2(clear), .pin3(_7474_1_pin1), .pin4(1'b0), .pin5(1'b0), .pin7(1'b0), .pin9(1'b0),
    .pin10(1'b0), .pin12(1'b0), .pin13(1'b0), .pin14(1'b1));  // open: pin6, pin8, pin11
  _7400 _7400_3 (
    .pin1(T0), .pin2(_7408_5_pin3), .pin3(_7400_3_pin3), .pin4(_7400_3_pin4), .pin5(_7400_3_pin5),
    .pin6(out_13), .pin7(1'b0), .pin8(_7400_3_pin5), .pin9(_7408_5_pin3), .pin10(_7400_3_pin3),
    .pin11(_7400_3_pin4), .pin12(T0), .pin13(_7400_3_pin3), .pin14(1'b1));
  _7432 _7432_1 (
    .pin1(D0), .pin2(D1), .pin3(_7432_1_pin3), .pin4(D2), .pin5(D3), .pin6(_7432_1_pin6), .pin7(1'b0),
    .pin8(_7432_1_pin8), .pin9(D4), .pin10(D5), .pin11(_7432_1_pin11), .pin12(D6), .pin13(D7), .pin14(1'b1));
  _7432 _7432_2 (
    .pin1(_7432_1_pin6), .pin2(_7432_1_pin3), .pin3(_7432_2_pin3), .pin4(_7432_1_pin11), .pin5(_7432_1_pin8),
    .pin6(_7432_2_pin6), .pin7(1'b0), .pin8(out_9), .pin9(_7432_2_pin6), .pin10(_7432_2_pin3),
    .pin12(_7432_2_pin3), .pin13(_7432_2_pin3), .pin14(1'b1));  // open: pin11
endmodule
