// Digital circuit jelly-seven-loops.dig as structural Verilog
module jelly_seven_loops (
  input  M0,
  input  M1,
  input  M2,
  input  M3,
  input  begin_2,
  input  again_2,
  input  zero,
  input  mode,
  input  move,
  input  D0,
  input  D1,
  input  D2,
  input  D3,
  input  D4,
  input  D5,
  input  D6,
  input  D7,
  input  move_3,
  input  T2,
  input  T3,
  input  T2_2,
  input  T3_2,
  output Y0,
  output Y1,
  output Y2,
  output Y3,
  output Y4,
  output Y5,
  output Y6,
  output Y7,
  output OE6,
  output CLK4,
  output CLK5,
  output CLR4,
  output CLR3,
  output \begin ,
  output again,
  output zero_2,
  output mode_2,
  output move_2,
  output F_B,
  output R_W
);

  wire and_2_out, and_3_out, and_4_out, and_5_out, and_6_out, and_7_out, and_8_out, and_9_out, d_ff_1_nq,
       d_ff_2_nq, nand_1_out, nand_2_out, nand_4_out, nand_5_out, nand_6_out, or_1_out, or_2_out, or_3_out,
       or_4_out, or_5_out, or_6_out, or_8_out, or_9_out, or_10_out;

  or or_1 (or_1_out, D0, D1);
  or or_2 (or_2_out, D2, D3);
  or or_3 (or_3_out, D4, D5);
  or or_4 (or_4_out, D6, D7);
  and and_1 (R_W, T2_2, T3_2);
  and and_2 (and_2_out, move_3, T2);
  or or_5 (or_5_out, or_1_out, or_2_out);
  or or_6 (or_6_out, or_3_out, or_4_out);
  nand nand_1 (nand_1_out, zero, zero);
  nand nand_2 (nand_2_out, mode, mode);
  xor xor_1 (F_B, and_2_out, T3);
  or or_7 (zero_2, or_5_out, or_6_out);
  and and_3 (and_3_out, begin_2, nand_1_out);
  and and_4 (and_4_out, again_2, zero);
  and and_5 (and_5_out, mode, move);
  and and_6 (and_6_out, nand_2_out, and_3_out);
  and and_7 (and_7_out, nand_2_out, and_4_out);
  and and_8 (and_8_out, nand_1_out, mode);
  or or_8 (or_8_out, and_6_out, and_7_out);
  or or_9 (or_9_out, or_8_out, and_8_out);
  or or_10 (or_10_out, and_7_out, and_5_out);
  D_FF d_ff_1 (.D(d_ff_1_nq), .C(or_9_out), .Q(mode_2), .nQ(d_ff_1_nq));
  D_FF d_ff_2 (.D(d_ff_2_nq), .C(or_10_out), .Q(move_2), .nQ(d_ff_2_nq));
  _74138 _74138_1 (
    .pin1(M0), .pin2(M1), .pin3(M2), .pin4(M3), .pin5(1'b0), .pin6(1'b1), .pin7(Y7), .pin8(1'b0), .pin9(Y6),
    .pin10(CLR4), .pin11(Y4), .pin12(Y3), .pin13(Y2), .pin14(Y1), .pin15(Y0), .pin16(1'b1));
  and and_9 (and_9_out, Y1, Y2);
  nand nand_3 (CLK4, Y2, Y2);
  nand nand_4 (nand_4_out, Y3, Y3);
  nand nand_5 (nand_5_out, Y4, Y4);
  nand nand_6 (nand_6_out, CLR4, CLR4);
  and and_10 (OE6, and_9_out, Y3);
  or or_11 (CLK5, nand_4_out, nand_5_out);
  or or_12 (CLR3, CLK4, nand_6_out);
  nand nand_7 (\begin , Y6, Y6);
  nand nand_8 (again, Y7, Y7);

  assign Y5 = CLR4;
endmodule
