// Digital circuit jelly-seven-loops.x.dig as structural Verilog
module jelly_seven_loops_x (
  input  \begin ,
  input  again,
  input  zero,
  input  mode,
  input  D0,
  input  D1,
  input  D2,
  input  D3,
  input  D4,
  input  D5,
  input  D6,
  input  D7,
  input  K0,
  input  K1,
  input  move_2,
  output mode_2,
  output move,
  output out_17,
  output zero_2
);

  wire d_ff_1_nq, d_ff_2_nq, nand_1_out, nand_2_out, nand_3_out, nand_4_out, nand_5_out, nand_6_out,
       nand_7_out, nand_8_out, nand_9_out, nand_10_out, nand_11_out, nand_12_out, nand_13_out, nand_14_out,
       nand_15_out, nand_16_out, nand_17_out, nand_18_out, nand_19_out, or_1_out, or_2_out, or_3_out,
       or_4_out, or_5_out, or_6_out, or_8_out, or_9_out, or_10_out;

  or or_1 (or_1_out, D0, D1);
  or or_2 (or_2_out, D2, D3);
  or or_3 (or_3_out, D4, D5);
  or or_4 (or_4_out, D6, D7);
  or or_5 (or_5_out, or_1_out, or_2_out);
  or or_6 (or_6_out, or_3_out, or_4_out);
  nand nand_1 (nand_1_out, zero, zero);
  nand nand_2 (nand_2_out, mode_2, mode_2);
  nand nand_3 (nand_3_out, move_2, K0);
  or or_7 (zero_2, or_5_out, or_6_out);
  nand nand_4 (nand_4_out, nand_3_out, nand_3_out);
  nand nand_5 (nand_5_out, \begin , nand_1_out);
  nand nand_6 (nand_6_out, again, zero);
  nand nand_7 (nand_7_out, nand_1_out, mode_2);
  nand nand_8 (nand_8_out, nand_5_out, nand_5_out);
  nand nand_9 (nand_9_out, nand_6_out, nand_6_out);
  nand nand_10 (nand_10_out, nand_7_out, nand_7_out);
  nand nand_11 (nand_11_out, nand_8_out, nand_2_out);
  nand nand_12 (nand_12_out, nand_9_out, nand_2_out);
  nand nand_13 (nand_13_out, nand_10_out, move);
  nand nand_14 (nand_14_out, nand_4_out, K1);
  nand nand_15 (nand_15_out, nand_11_out, nand_11_out);
  nand nand_16 (nand_16_out, nand_12_out, nand_12_out);
  nand nand_17 (nand_17_out, nand_13_out, nand_13_out);
  nand nand_18 (nand_18_out, nand_4_out, nand_14_out);
  nand nand_19 (nand_19_out, nand_14_out, K1);
  or or_8 (or_8_out, nand_15_out, nand_16_out);
  or or_9 (or_9_out, nand_16_out, nand_17_out);
  nand nand_20 (out_17, nand_18_out, nand_19_out);
  D_FF d_ff_1 (.D(d_ff_1_nq), .C(or_9_out), .Q(move), .nQ(d_ff_1_nq));
  or or_10 (or_10_out, or_8_out, nand_10_out);
  D_FF d_ff_2 (.D(d_ff_2_nq), .C(or_10_out), .Q(mode_2), .nQ(d_ff_2_nq));
endmodule
