// Digital circuit jelly-seven.dig as structural Verilog
module jelly_seven (
  input  clock,
  input  halt,
  input  MOVE,
  input  T2,
  input  T3,
  output FW_BK
);

  wire _7400_1_pin3, _7400_2_pin1, _7400_2_pin2, _7400_2_pin3, _7400_2_pin4, _7400_2_pin6, _7400_2_pin8,
       _7408_1_pin7, _7408_1_pin14, _7408_2_pin3, _7408_2_pin6, _7432_1_pin3, _7432_1_pin6, _7432_1_pin8,
       _7432_1_pin11, _7432_2_pin3, _7432_2_pin6, _7432_2_pin8, _7474_1_pin2, _7474_1_pin5, _7474_1_pin8,
       _7474_1_pin9, and_1_out, and_2_out, not_1_out;
  wire [2:0] U1_p11, U1_p14, U3_p9, U3_p14;
  wire [3:0] pulldown_12_out, pulldown_29_out, U2_p11;
  wire [3:3] U6_pin11;
  wire [7:0] U4_pin2, U5_pin19, U7_pin18, U8_74HC393_pin3;
  wire [7:3] U3_p20;

  not not_1 (not_1_out, halt);
  LED led_1 (.in(not_1_out));
  LED led_2 (.in(clock));
  _74574 U4 (
    .pin1(1'b0), .pin2(U4_pin2[0]), .pin3(U4_pin2[1]), .pin4(U4_pin2[2]), .pin5(U4_pin2[3]),
    .pin6(U4_pin2[4]), .pin7(U4_pin2[5]), .pin8(U4_pin2[6]), .pin9(U4_pin2[7]), .pin10(1'b0),
    .pin11(U2_p11[0]), .pin16(U8_74HC393_pin3[7]), .pin17(U8_74HC393_pin3[6]), .pin18(U8_74HC393_pin3[5]),
    .pin19(U8_74HC393_pin3[4]), .pin20(1'b1));  // open: pin12, pin13, pin14, pin15
  and and_1 (and_1_out, clock, not_1_out);
  _74574 U5 (
    .pin1(1'b0), .pin2(U4_pin2[0]), .pin3(U4_pin2[1]), .pin4(U4_pin2[2]), .pin5(U4_pin2[3]),
    .pin6(U4_pin2[4]), .pin7(U4_pin2[5]), .pin8(U4_pin2[6]), .pin9(U4_pin2[7]), .pin10(1'b0),
    .pin11(U2_p11[1]), .pin12(U5_pin19[7]), .pin13(U5_pin19[6]), .pin14(U5_pin19[5]), .pin15(U5_pin19[4]),
    .pin16(U5_pin19[3]), .pin17(U5_pin19[2]), .pin18(U5_pin19[1]), .pin19(U5_pin19[0]), .pin20(1'b1));
  _74193 U8_74HC393 (
    .pin2(U8_74HC393_pin3[1]), .pin3(U8_74HC393_pin3[0]), .pin5(and_1_out), .pin6(U8_74HC393_pin3[2]),
    .pin7(U8_74HC393_pin3[3]), .pin8(1'b0), .pin16(1'b1));  // open: pin1, pin4, pin9, pin10, pin11, pin12, pin13, pin14, pin15
  // _28c16 U1: pin names not known; wires that end beside it: U8_74HC393_pin3[7], U8_74HC393_pin3[6], U8_74HC393_pin3[5], U8_74HC393_pin3[4], U8_74HC393_pin3[3], U8_74HC393_pin3[2], U8_74HC393_pin3[1], U8_74HC393_pin3[0], U1_p11[0], U1_p11[1], U1_p11[2], 1'b0, 1'b1, U1_p14[0], U1_p14[1], 1'b1, 1'b0, U1_p14[2], 1'b0, pulldown_12_out[3], pulldown_12_out[2], pulldown_12_out[1]
  // _28c16 U3: pin names not known; wires that end beside it: U5_pin19[7], U5_pin19[6], U5_pin19[5], U5_pin19[4], U5_pin19[3], U5_pin19[2], U5_pin19[1], U5_pin19[0], U3_p9[0], U3_p9[1], U3_p9[2], 1'b0, 1'b1, U3_p14[0], U3_p14[1], 1'b1, 1'b0, U3_p14[2], 1'b0, U3_p20[7], U3_p20[6], U3_p20[5]
  // _28c16 U2: pin names not known; wires that end beside it: U8_74HC393_pin3[7], U8_74HC393_pin3[6], U8_74HC393_pin3[5], U8_74HC393_pin3[4], U8_74HC393_pin3[3], U8_74HC393_pin3[2], U8_74HC393_pin3[1], U8_74HC393_pin3[0], U2_p11[0], U2_p11[1], U2_p11[2], 1'b0, 1'b1, U1_p14[0], U1_p14[1], 1'b1, 1'b0, U1_p14[2], 1'b0, pulldown_29_out[3], pulldown_29_out[2], pulldown_29_out[1]
  _74574 U6 (
    .pin1(U2_p11[2]), .pin2(U3_p9[0]), .pin3(U3_p9[1]), .pin4(U3_p9[2]), .pin5(U3_p20[3]), .pin6(U3_p20[4]),
    .pin7(U3_p20[5]), .pin8(U3_p20[6]), .pin9(U3_p20[7]), .pin10(1'b0), .pin11(U6_pin11[3]),
    .pin12(U4_pin2[7]), .pin13(U4_pin2[6]), .pin14(U4_pin2[5]), .pin15(U4_pin2[4]), .pin16(U4_pin2[3]),
    .pin17(U4_pin2[2]), .pin18(U4_pin2[1]), .pin19(U4_pin2[0]), .pin20(1'b1));
  _7408 _7408_1 (
    .pin1(U6_pin11[3]), .pin2(U1_p11[2]), .pin3(U3_p14[2]), .pin4(U6_pin11[3]), .pin5(U1_p11[1]),
    .pin6(U3_p14[1]), .pin7(_7408_1_pin7), .pin8(U3_p14[0]), .pin9(U6_pin11[3]), .pin10(U1_p11[0]),
    .pin14(_7408_1_pin14));  // open: pin11, pin12, pin13
  _74245 U7 (
    .pin1(FW_BK), .pin2(U4_pin2[0]), .pin3(U4_pin2[1]), .pin4(U4_pin2[2]), .pin5(U4_pin2[3]),
    .pin6(U4_pin2[4]), .pin7(U4_pin2[5]), .pin8(U4_pin2[6]), .pin9(U4_pin2[7]), .pin10(1'b0),
    .pin11(U7_pin18[7]), .pin12(U7_pin18[6]), .pin13(U7_pin18[5]), .pin14(U7_pin18[4]), .pin15(U7_pin18[3]),
    .pin16(U7_pin18[2]), .pin17(U7_pin18[1]), .pin18(U7_pin18[0]), .pin19(U2_p11[3]), .pin20(1'b1));
  _7400 _7400_1 (
    .pin1(U6_pin11[3]), .pin2(U6_pin11[3]), .pin3(_7400_1_pin3), .pin7(_7408_1_pin7), .pin14(_7408_1_pin14));  // open: pin4, pin5, pin6, pin8, pin9, pin10, pin11, pin12, pin13
  _7408 _7408_2 (
    .pin1(_7400_1_pin3), .pin2(U1_p11[2]), .pin3(_7408_2_pin3), .pin4(_7400_1_pin3), .pin5(U1_p11[1]),
    .pin6(_7408_2_pin6), .pin7(_7408_1_pin7), .pin9(_7400_1_pin3), .pin10(U1_p11[0]), .pin14(_7408_1_pin14));  // open: pin8, pin11, pin12, pin13
  LED A0 (.in(U8_74HC393_pin3[0]));
  PullDown pulldown_1 (.out(U8_74HC393_pin3[0]));
  LED M0 (.in(U1_p11[0]));
  PullDown pulldown_2 (.out(U1_p11[0]));
  _7474 _7474_1 (
    .pin2(_7474_1_pin2), .pin3(_7408_2_pin3), .pin5(_7474_1_pin5), .pin6(_7474_1_pin2), .pin7(_7408_1_pin7),
    .pin8(_7474_1_pin8), .pin9(_7474_1_pin9), .pin11(_7408_2_pin6), .pin12(_7474_1_pin8),
    .pin14(_7408_1_pin14));  // open: pin1, pin4, pin10, pin13
  LED A1 (.in(U8_74HC393_pin3[1]));
  LED A2 (.in(U8_74HC393_pin3[2]));
  PullDown pulldown_3 (.out(U8_74HC393_pin3[1]));
  PullDown pulldown_4 (.out(U8_74HC393_pin3[2]));
  LED M1 (.in(U1_p11[1]));
  LED M2 (.in(U1_p11[2]));
  PullDown pulldown_5 (.out(U1_p11[1]));
  PullDown pulldown_6 (.out(U1_p11[2]));
  LED D0 (.in(U4_pin2[0]));
  LED D1 (.in(U4_pin2[1]));
  PullDown pulldown_7 (.out(U4_pin2[0]));
  PullDown pulldown_8 (.out(U4_pin2[1]));
  LED A3 (.in(U8_74HC393_pin3[3]));
  LED A4 (.in(U8_74HC393_pin3[4]));
  PullDown pulldown_9 (.out(U8_74HC393_pin3[3]));
  PullDown pulldown_10 (.out(U8_74HC393_pin3[4]));
  LED M3 (.in(U6_pin11[3]));
  LED T0 (.in(pulldown_12_out[0]));
  PullDown pulldown_11 (.out(U6_pin11[3]));
  PullDown pulldown_12 (.out(pulldown_12_out[0]));
  LED D2 (.in(U4_pin2[2]));
  LED D3 (.in(U4_pin2[3]));
  PullDown pulldown_13 (.out(U4_pin2[2]));
  PullDown pulldown_14 (.out(U4_pin2[3]));
  LED A5 (.in(U8_74HC393_pin3[5]));
  LED A6 (.in(U8_74HC393_pin3[6]));
  PullDown pulldown_15 (.out(U8_74HC393_pin3[5]));
  PullDown pulldown_16 (.out(U8_74HC393_pin3[6]));
  LED T1 (.in(pulldown_12_out[1]));
  LED u_T2 (.in(pulldown_12_out[2]));
  PullDown pulldown_17 (.out(pulldown_12_out[1]));
  PullDown pulldown_18 (.out(pulldown_12_out[2]));
  LED D4 (.in(U4_pin2[4]));
  LED D5 (.in(U4_pin2[5]));
  PullDown pulldown_19 (.out(U4_pin2[4]));
  PullDown pulldown_20 (.out(U4_pin2[5]));
  LED A7 (.in(U8_74HC393_pin3[7]));
  PullDown pulldown_21 (.out(U8_74HC393_pin3[7]));
  LED u_T3 (.in(pulldown_12_out[3]));
  PullDown pulldown_22 (.out(pulldown_12_out[3]));
  LED D6 (.in(U4_pin2[6]));
  LED D7 (.in(U4_pin2[7]));
  PullDown pulldown_23 (.out(U4_pin2[6]));
  PullDown pulldown_24 (.out(U4_pin2[7]));
  _7400 _7400_2 (
    .pin1(_7400_2_pin1), .pin2(_7400_2_pin2), .pin3(_7400_2_pin3), .pin4(_7400_2_pin4), .pin5(_7400_2_pin2),
    .pin6(_7400_2_pin6), .pin8(_7400_2_pin8), .pin9(_7400_2_pin3), .pin10(_7400_2_pin6),
    .pin11(_7400_2_pin2), .pin12(_7400_2_pin1), .pin13(_7400_2_pin4));  // open: pin7, pin14
  LED C0 (.in(U2_p11[0]));
  PullDown pulldown_25 (.out(U2_p11[0]));
  _7432 _7432_1 (
    .pin1(U4_pin2[0]), .pin2(U4_pin2[1]), .pin3(_7432_1_pin3), .pin4(U4_pin2[2]), .pin5(U4_pin2[3]),
    .pin6(_7432_1_pin6), .pin7(1'b0), .pin8(_7432_1_pin8), .pin9(U4_pin2[7]), .pin10(U4_pin2[6]),
    .pin11(_7432_1_pin11), .pin12(U4_pin2[5]), .pin13(U4_pin2[4]), .pin14(1'b1));
  LED C1 (.in(U2_p11[1]));
  LED C2 (.in(U2_p11[2]));
  PullDown pulldown_26 (.out(U2_p11[1]));
  PullDown pulldown_27 (.out(U2_p11[2]));
  and and_2 (and_2_out, MOVE, T2);
  LED C3 (.in(U2_p11[3]));
  LED K1 (.in(pulldown_29_out[0]));
  PullDown pulldown_28 (.out(U2_p11[3]));
  PullDown pulldown_29 (.out(pulldown_29_out[0]));
  LED K2 (.in(pulldown_29_out[1]));
  LED K3 (.in(pulldown_29_out[2]));
  PullDown pulldown_30 (.out(pulldown_29_out[1]));
  PullDown pulldown_31 (.out(pulldown_29_out[2]));
  xor xor_1 (FW_BK, and_2_out, T3);
  LED K4 (.in(pulldown_29_out[3]));
  PullDown pulldown_32 (.out(pulldown_29_out[3]));
  _7432 _7432_2 (
    .pin1(_7432_1_pin3), .pin2(_7432_1_pin6), .pin3(_7432_2_pin3), .pin4(_7432_1_pin11), .pin5(_7432_1_pin8),
    .pin6(_7432_2_pin6), .pin7(1'b0), .pin8(_7432_2_pin8), .pin9(_7432_2_pin6), .pin10(_7432_2_pin3),
    .pin14(1'b1));  // open: pin11, pin12, pin13

  // Notes on the sheet:
  //   opcode counter
  //   FSM Bus
  //   pipeline counter
  //   M0-M3
  //   T0-T3
  //   C0-C3
  //   Address Bus
  //   Signal Bus
  //   Data Bus
  //   Reverse Move
  //   Control Bus
  //   Zero Detector
endmodule
