// Digital circuit jelly-six-halt.dig as structural Verilog
module jelly_six_halt (
  input  one,
  input  two,
  input  swap,
  input  fw,
  input  bk,
  input  move,
  input  M1,
  input  M2,
  input  OE4,
  input  oe4_2,
  input  m1_2,
  input  one_3,
  input  two_3,
  input  fw_3,
  input  bk_3,
  input  m2_2,
  output ONE_2,
  output TWO_2,
  output FW_2,
  output BK_2,
  output swap_2,
  output move_2,
  output swap_3,
  output TWO_4,
  output ONE_4,
  output FW_4,
  output BK_4,
  output move_3
);

  wire _7400_1_pin8, _7408_1_pin4, _7408_1_pin5, _7408_1_pin6, _7408_1_pin8, _7408_1_pin9, _7408_1_pin10,
       _7474_1_pin6, _7474_1_pin8, _7486_1_pin3, _7486_1_pin13, and_1_out, and_4_out, d_ff_1_nq, d_ff_1_q,
       d_ff_2_nq, d_ff_2_q, nand_1_out, xor_1_out, xor_2_out, xor_5_out, xor_6_out;

  _7400 _7400_1 (
    .pin1(1'b0), .pin2(1'b0), .pin4(1'b0), .pin5(1'b0), .pin7(1'b0), .pin8(_7400_1_pin8), .pin9(oe4_2),
    .pin10(oe4_2), .pin12(1'b1), .pin13(1'b1), .pin14(1'b1));  // open: pin3, pin6, pin11
  _7408 _7408_1 (
    .pin1(m2_2), .pin2(_7400_1_pin8), .pin3(move_3), .pin4(_7408_1_pin4), .pin5(_7408_1_pin5),
    .pin6(_7408_1_pin6), .pin7(1'b0), .pin8(_7408_1_pin8), .pin9(_7408_1_pin9), .pin10(_7408_1_pin10),
    .pin11(swap_3), .pin12(_7400_1_pin8), .pin13(m1_2), .pin14(1'b1));
  _7486 _7486_1 (
    .pin1(1'b1), .pin2(_7408_1_pin4), .pin3(_7486_1_pin3), .pin4(fw_3), .pin5(bk_3), .pin6(_7408_1_pin5),
    .pin7(1'b0), .pin8(_7408_1_pin10), .pin9(two_3), .pin10(one_3), .pin11(_7408_1_pin9), .pin12(1'b1),
    .pin13(_7486_1_pin13), .pin14(1'b1));
  _7474 _7474_1 (
    .pin1(1'b1), .pin2(_7486_1_pin3), .pin3(move_3), .pin4(1'b1), .pin5(_7408_1_pin4), .pin6(_7474_1_pin6),
    .pin7(1'b0), .pin8(_7474_1_pin8), .pin9(_7486_1_pin13), .pin10(1'b1), .pin11(swap_3),
    .pin12(_7408_1_pin9), .pin13(1'b1), .pin14(1'b1));
  _7486 _7486_2 (
    .pin1(fw_3), .pin2(_7408_1_pin6), .pin3(FW_4), .pin4(bk_3), .pin5(_7408_1_pin6), .pin6(BK_4),
    .pin7(1'b0), .pin8(ONE_4), .pin9(one_3), .pin10(_7408_1_pin8), .pin11(TWO_4), .pin12(two_3),
    .pin13(_7408_1_pin8), .pin14(1'b1));
  LED led_1 (.in(_7474_1_pin8));
  LED led_2 (.in(_7474_1_pin6));
  LED led_3 (.in(swap));
  xor xor_1 (xor_1_out, d_ff_1_q, 1'b1);
  xor xor_2 (xor_2_out, one, two);
  xor xor_3 (ONE_2, and_1_out, one);
  xor xor_4 (TWO_2, and_1_out, two);
  nand nand_1 (nand_1_out, OE4, OE4);
  D_FF d_ff_1 (.D(xor_1_out), .C(swap), .Q(d_ff_1_q), .nQ(d_ff_1_nq));
  and and_1 (and_1_out, d_ff_1_q, xor_2_out);
  LED led_4 (.in(d_ff_1_nq));
  and and_2 (swap_2, nand_1_out, M1);
  and and_3 (move_2, nand_1_out, M2);
  LED led_5 (.in(move));
  xor xor_5 (xor_5_out, d_ff_2_q, 1'b1);
  xor xor_6 (xor_6_out, fw, bk);
  xor xor_7 (FW_2, and_4_out, fw);
  xor xor_8 (BK_2, and_4_out, bk);
  and and_4 (and_4_out, d_ff_2_q, xor_6_out);
  D_FF d_ff_2 (.D(xor_5_out), .C(move), .Q(d_ff_2_q), .nQ(d_ff_2_nq));
  LED led_6 (.in(d_ff_2_nq));
endmodule
