// Digital circuit jelly-six.dig as structural Verilog
module jelly_six (
  input  clock,
  input  halt,
  input  D0,
  input  D1,
  input  D2,
  input  D3,
  input  D4,
  input  D5,
  input  D6,
  input  D7,
  input  m1_2,
  input  one_2,
  input  two_2,
  input  fw_2,
  input  bk_2,
  input  m2_2,
  output BOB,
  output one,
  output two,
  output RD,
  output WR,
  output fw,
  output bk,
  output HLT,
  output D0_2,
  output D1_2,
  output D2_2,
  output D3_2,
  output D4_2,
  output D5_2,
  output D6_2,
  output D7_2,
  output zero,
  output A0,
  output A1,
  output A2,
  output A3,
  output A4,
  output A5,
  output A6,
  output A7,
  output ce6,
  output oe4,
  output m2,
  output m1,
  output A8,
  output A9,
  output ce5,
  output oe2,
  output N4,
  output N3,
  output N2,
  output N1,
  output swap,
  output TWO_3,
  output ONE_3,
  output FW_3,
  output BK_3,
  output move
);

  wire not_1_out, U1_p11, U1_p22, u7_pin5, u7_pin12, u7_pin13, u8_pin3, u8_pin6, u8_pin8, u8_pin13, u9_pin3,
       u9_pin6, u11_pin4, u11_pin5, u11_pin6, u11_pin8, u11_pin9, u11_pin10, u12_pin3, u12_pin13, u13_pin6,
       u13_pin8;
  wire [7:0] u5_pin2, u5_pin19, u6_pin19;

  LED led_1 (.in(A0));
  PullDown pulldown_1 (.out(A0));
  LED led_2 (.in(A2));
  LED led_3 (.in(A1));
  PullDown pulldown_2 (.out(A1));
  PullDown pulldown_3 (.out(A2));
  LED led_4 (.in(A4));
  LED led_5 (.in(A3));
  PullDown pulldown_4 (.out(A3));
  PullDown pulldown_5 (.out(A4));
  LED led_6 (.in(A6));
  LED led_7 (.in(A5));
  PullDown pulldown_6 (.out(A5));
  PullDown pulldown_7 (.out(A6));
  LED led_8 (.in(A7));
  PullDown pulldown_8 (.out(A7));
  LED led_9 (.in(m1_2));
  PullDown pulldown_9 (.out(m1_2));
  LED led_10 (.in(N1));
  PullDown pulldown_10 (.out(N1));
  LED led_11 (.in(oe4));
  LED led_12 (.in(m2_2));
  PullDown pulldown_11 (.out(m2_2));
  PullDown pulldown_12 (.out(oe4));
  LED led_13 (.in(N3));
  LED led_14 (.in(N2));
  PullDown pulldown_13 (.out(N2));
  PullDown pulldown_14 (.out(N3));
  LED led_15 (.in(ce6));
  PullDown pulldown_15 (.out(ce6));
  LED led_16 (.in(N4));
  PullDown pulldown_16 (.out(N4));
  _74574 u5 (
    .pin1(ce6), .pin2(u5_pin2[0]), .pin3(u5_pin2[1]), .pin4(u5_pin2[2]), .pin5(u5_pin2[3]),
    .pin6(u5_pin2[4]), .pin7(u5_pin2[5]), .pin8(u5_pin2[6]), .pin9(u5_pin2[7]), .pin10(ce6), .pin11(ce5),
    .pin12(u5_pin19[7]), .pin13(u5_pin19[6]), .pin14(u5_pin19[5]), .pin15(u5_pin19[4]), .pin16(u5_pin19[3]),
    .pin17(u5_pin19[2]), .pin18(u5_pin19[1]), .pin19(u5_pin19[0]), .pin20(1'b1));
  _74574 u6 (
    .pin1(ce6), .pin2(u5_pin2[0]), .pin3(u5_pin2[1]), .pin4(u5_pin2[2]), .pin5(u5_pin2[3]),
    .pin6(u5_pin2[4]), .pin7(u5_pin2[5]), .pin8(u5_pin2[6]), .pin9(u5_pin2[7]), .pin10(ce6), .pin11(ce6),
    .pin12(u6_pin19[7]), .pin13(u6_pin19[6]), .pin14(u6_pin19[5]), .pin15(u6_pin19[4]), .pin16(u6_pin19[3]),
    .pin17(u6_pin19[2]), .pin18(u6_pin19[1]), .pin19(u6_pin19[0]), .pin20(1'b1));
  // _28c16 U1: pin names not known; wires that end beside it: A7, A6, A5, A4, A3, A2, A1, A0, m1_2, m2_2, U1_p11, ce6, 1'b1, A9, A8, 1'b1, ce6, ce6, ce6, A8, A9, U1_p22
  // _28c16 U2: pin names not known; wires that end beside it: A7, A6, A5, A4, A3, A2, A1, A0, BOB, one, two, ce6, 1'b1, A9, A8, 1'b1, oe2, ce6, ce6, HLT, bk, fw
  // _28c16 u3: pin names not known; wires that end beside it: u5_pin19[7], u5_pin19[6], u5_pin19[5], u5_pin19[4], u5_pin19[3], u5_pin19[2], u5_pin19[1], u5_pin19[0], N1, N2, N3, ce6, 1'b1, ce6, ce6, 1'b1, ce6, ce6, ce6, A7, A6, A5
  // _28c16 u4: pin names not known; wires that end beside it: u6_pin19[7], u6_pin19[6], u6_pin19[5], u6_pin19[4], u6_pin19[3], u6_pin19[2], u6_pin19[1], u6_pin19[0], u5_pin2[0], u5_pin2[1], u5_pin2[2], ce6, 1'b1, m1_2, m2_2, 1'b1, oe4, ce6, ce6, u5_pin2[7], u5_pin2[6], u5_pin2[5]
  LED led_17 (.in(A9));
  LED led_18 (.in(A8));
  PullDown pulldown_17 (.out(A9));
  PullDown pulldown_18 (.out(A8));
  LED led_19 (.in(one));
  LED led_20 (.in(BOB));
  PullDown pulldown_19 (.out(BOB));
  PullDown pulldown_20 (.out(one));
  LED led_21 (.in(oe2));
  LED led_22 (.in(ce5));
  PullDown pulldown_21 (.out(oe2));
  PullDown pulldown_22 (.out(ce5));
  LED led_23 (.in(RD));
  LED led_24 (.in(two));
  PullDown pulldown_23 (.out(two));
  PullDown pulldown_24 (.out(RD));
  LED led_25 (.in(fw));
  LED led_26 (.in(WR));
  PullDown pulldown_25 (.out(WR));
  PullDown pulldown_26 (.out(fw));
  _7432 u8 (
    .pin1(u5_pin2[0]), .pin2(u5_pin2[1]), .pin3(u8_pin3), .pin4(u5_pin2[2]), .pin5(u5_pin2[3]),
    .pin6(u8_pin6), .pin7(1'b0), .pin8(u8_pin8), .pin9(u8_pin6), .pin10(u8_pin3), .pin11(zero),
    .pin12(u8_pin8), .pin13(u8_pin13), .pin14(1'b1));
  _7432 u9 (
    .pin1(u5_pin2[4]), .pin2(u5_pin2[5]), .pin3(u9_pin3), .pin4(u5_pin2[6]), .pin5(u5_pin2[7]),
    .pin6(u9_pin6), .pin7(1'b0), .pin8(u8_pin13), .pin9(u9_pin6), .pin10(u9_pin3), .pin12(1'b1),
    .pin13(1'b1), .pin14(1'b1));  // open: pin11
  LED led_27 (.in(HLT));
  LED led_28 (.in(bk));
  PullDown pulldown_27 (.out(bk));
  PullDown pulldown_28 (.out(HLT));
  _74193 u7 (
    .pin1(ce6), .pin2(A1), .pin3(A0), .pin4(1'b1), .pin5(u7_pin5), .pin6(A2), .pin7(A3), .pin8(ce6),
    .pin9(ce6), .pin10(ce6), .pin11(1'b1), .pin12(u7_pin12), .pin13(u7_pin13), .pin14(ce5), .pin15(ce6),
    .pin16(1'b1));
  LED led_29 (.in(u7_pin13));
  LED led_30 (.in(u7_pin12));
  LED led_31 (.in(ce5));
  LED led_32 (.in(zero));
  LED led_33 (.in(clock));
  not not_1 (not_1_out, halt);
  LED led_34 (.in(not_1_out));
  and and_1 (u7_pin5, clock, not_1_out);
  LED led_35 (.in(D1));
  LED led_36 (.in(D0));
  PullDown pulldown_29 (.out(D0));
  PullDown pulldown_30 (.out(D1));
  LED led_37 (.in(D3));
  LED led_38 (.in(D2));
  PullDown pulldown_31 (.out(D2));
  PullDown pulldown_32 (.out(D3));
  LED led_39 (.in(D5));
  LED led_40 (.in(D4));
  PullDown pulldown_33 (.out(D4));
  PullDown pulldown_34 (.out(D5));
  LED led_41 (.in(D7));
  LED led_42 (.in(D6));
  PullDown pulldown_35 (.out(D6));
  PullDown pulldown_36 (.out(D7));
  _7400 u10 (
    .pin1(U1_p22), .pin2(U1_p22), .pin3(oe2), .pin4(U1_p11), .pin5(U1_p11), .pin6(oe4), .pin7(1'b0),
    .pin9(1'b1), .pin10(1'b1), .pin12(1'b1), .pin13(1'b1), .pin14(1'b1));  // open: pin8, pin11
  _7408 u11 (
    .pin1(m2_2), .pin2(oe4), .pin3(move), .pin4(u11_pin4), .pin5(u11_pin5), .pin6(u11_pin6), .pin7(1'b0),
    .pin8(u11_pin8), .pin9(u11_pin9), .pin10(u11_pin10), .pin11(swap), .pin12(oe4), .pin13(m1_2), .pin14(1'b1));
  _7486 u12 (
    .pin1(1'b1), .pin2(u11_pin4), .pin3(u12_pin3), .pin4(fw_2), .pin5(bk_2), .pin6(u11_pin5), .pin7(1'b0),
    .pin8(u11_pin10), .pin9(two_2), .pin10(one_2), .pin11(u11_pin9), .pin12(1'b1), .pin13(u12_pin13),
    .pin14(1'b1));
  _7474 u13 (
    .pin1(1'b1), .pin2(u12_pin3), .pin3(move), .pin4(1'b1), .pin5(u11_pin4), .pin6(u13_pin6), .pin7(1'b0),
    .pin8(u13_pin8), .pin9(u12_pin13), .pin10(1'b1), .pin11(swap), .pin12(u11_pin9), .pin13(1'b1),
    .pin14(1'b1));
  _7486 u14 (
    .pin1(fw_2), .pin2(u11_pin6), .pin3(FW_3), .pin4(bk_2), .pin5(u11_pin6), .pin6(BK_3), .pin7(1'b0),
    .pin8(ONE_3), .pin9(one_2), .pin10(u11_pin8), .pin11(TWO_3), .pin12(two_2), .pin13(u11_pin8), .pin14(1'b1));
  LED led_43 (.in(u13_pin8));
  LED led_44 (.in(u13_pin6));

  assign D0_2 = D0;
  assign D1_2 = D1;
  assign D2_2 = D2;
  assign D3_2 = D3;
  assign D4_2 = D4;
  assign D5_2 = D5;
  assign D6_2 = D6;
  assign D7_2 = D7;
  assign m1 = m1_2;
  assign m2 = m2_2;
  // also tied to GND on the sheet: ce6

  // Notes on the sheet:
  //   Decoder eeprom, translate a byte from ASCII into a valid BF instruction, ignores non valid;
  //   Code control eeprom, does  control logic of finite states for execute the current instruction;
  //   Tape control eeprom, selects which tape is active for use the Data bus and defines modes;
  //   Math operator eeprom, perform all math operations as table lookups;
  //   m1, m2, control math operation
  //   oe4 control output enable
  //   cs6 control output enable
  //   Data Bus is shared by all tapes
  //   Address Bus
  //   Data Bus
  //   FSM Bus
  //   code control eeprom
  //   tape control eeprom
  //   decoder eeprom
  //   lookup math eeprom
  //   A4-A7
  //   Zero detector
  //   Device Control
  //   A0-A3
  //   pipeline counter
  //   Basic Logic Level,
  //   check for fail states,
  //   does hold for swap tapes
  //   does hold for move direction
  //   could halt
endmodule
