// Digital circuit jelly-two-clear.dig as structural Verilog
module jelly_two_clear (
  input  CLEAR,
  input  [7:0] DATAIN,
  output [7:0] DATAOUT
);

  _7408 _7408_1 (
    .pin1(CLEAR), .pin2(DATAIN[0]), .pin3(DATAOUT[0]), .pin4(CLEAR), .pin5(DATAIN[1]), .pin6(DATAOUT[1]),
    .pin7(1'b0), .pin8(DATAOUT[2]), .pin9(CLEAR), .pin10(DATAIN[2]), .pin11(DATAOUT[3]), .pin12(CLEAR),
    .pin13(DATAIN[3]), .pin14(1'b1));
  _7408 _7408_2 (
    .pin1(CLEAR), .pin2(DATAIN[4]), .pin3(DATAOUT[4]), .pin4(CLEAR), .pin5(DATAIN[5]), .pin6(DATAOUT[5]),
    .pin7(1'b0), .pin8(DATAOUT[6]), .pin9(CLEAR), .pin10(DATAIN[6]), .pin11(DATAOUT[7]), .pin12(CLEAR),
    .pin13(DATAIN[7]), .pin14(1'b1));
endmodule
