// Digital circuit jelly-two-halt-chips.dig as structural Verilog
module jelly_two_halt_chips (
  input  rd,
  input  wr,
  input  fw,
  input  bk,
  input  bob,
  input  one,
  input  two,
  output bob_one_two,
  output bob_one,
  output bob_two,
  output one_two,
  output halt,
  output BOB_2,
  output ONE_2,
  output TWO_2
);

  wire _7408_1_pin2, _7408_3_pin3, _7408_3_pin6, _7408_3_pin8, _7408_3_pin11, _7408_4_pin3, _7408_4_pin6,
       _7432_1_pin3, _7432_1_pin6, _7432_1_pin8, _7432_1_pin11, _7432_1_pin12, _7432_1_pin13, _7432_2_pin6,
       _7432_2_pin8, _7486_1_pin2, _7486_1_pin3, _7486_1_pin6, _7486_1_pin8;

  _7486 _7486_1 (
    .pin1(one), .pin2(_7486_1_pin2), .pin3(_7486_1_pin3), .pin4(two), .pin5(_7486_1_pin2),
    .pin6(_7486_1_pin6), .pin7(1'b0), .pin8(_7486_1_pin8), .pin9(one), .pin10(two), .pin12(1'b1),
    .pin13(1'b1), .pin14(1'b1));  // open: pin11
  _7408 _7408_1 (
    .pin1(bob), .pin2(_7408_1_pin2), .pin3(BOB_2), .pin4(one), .pin5(_7408_1_pin2), .pin6(ONE_2),
    .pin7(1'b0), .pin8(TWO_2), .pin9(two), .pin10(_7408_1_pin2), .pin11(_7486_1_pin2), .pin12(_7486_1_pin8),
    .pin13(1'b1), .pin14(1'b1));
  _7408 _7408_2 (
    .pin1(bob), .pin2(_7486_1_pin3), .pin3(bob_one), .pin4(bob), .pin5(_7486_1_pin6), .pin6(bob_two),
    .pin7(1'b0), .pin8(bob_one_two), .pin9(bob_two), .pin10(bob_one), .pin11(one_two), .pin12(_7486_1_pin6),
    .pin13(_7486_1_pin3), .pin14(1'b1));
  _7432 _7432_1 (
    .pin1(bob_one), .pin2(bob_two), .pin3(_7432_1_pin3), .pin4(one_two), .pin5(bob_one_two),
    .pin6(_7432_1_pin6), .pin7(1'b0), .pin8(_7432_1_pin8), .pin9(_7432_1_pin6), .pin10(_7432_1_pin3),
    .pin11(_7432_1_pin11), .pin12(_7432_1_pin12), .pin13(_7432_1_pin13), .pin14(1'b1));
  _7400 _7400_1 (
    .pin1(_7432_1_pin8), .pin2(_7432_1_pin8), .pin3(_7408_1_pin2), .pin4(1'b0), .pin5(1'b0), .pin7(1'b0),
    .pin9(1'b1), .pin10(1'b1), .pin12(1'b1), .pin13(1'b1), .pin14(1'b1));  // open: pin6, pin8, pin11
  _7408 _7408_3 (
    .pin1(rd), .pin2(wr), .pin3(_7408_3_pin3), .pin4(fw), .pin5(bk), .pin6(_7408_3_pin6), .pin7(1'b0),
    .pin8(_7408_3_pin8), .pin9(fw), .pin10(rd), .pin11(_7408_3_pin11), .pin12(bk), .pin13(rd), .pin14(1'b1));
  _7408 _7408_4 (
    .pin1(wr), .pin2(fw), .pin3(_7408_4_pin3), .pin4(wr), .pin5(bk), .pin6(_7408_4_pin6), .pin7(1'b0),
    .pin8(halt), .pin9(_7408_1_pin2), .pin10(_7432_1_pin11), .pin12(1'b1), .pin13(1'b1), .pin14(1'b1));  // open: pin11
  _7432 _7432_2 (
    .pin1(_7408_3_pin3), .pin2(_7408_3_pin6), .pin3(_7432_1_pin12), .pin4(_7408_3_pin11),
    .pin5(_7408_3_pin8), .pin6(_7432_2_pin6), .pin7(1'b0), .pin8(_7432_2_pin8), .pin9(_7408_4_pin3),
    .pin10(_7408_4_pin6), .pin11(_7432_1_pin13), .pin12(_7432_2_pin6), .pin13(_7432_2_pin8), .pin14(1'b1));
  LED led_1 (.in(_7432_1_pin12));
  LED led_2 (.in(_7432_1_pin13));
endmodule
