// Digital circuit jelly-two-halt.dig as structural Verilog
module jelly_two_halt (
  input  rd,
  input  wr,
  input  fw,
  input  bk,
  input  bob,
  input  one,
  input  two,
  input  swap,
  input  rd_2,
  input  wr_2,
  input  fw_2,
  input  bk_2,
  input  bob_3,
  input  one_3,
  input  two_3,
  output halt,
  output BOB_2,
  output bob_one_two,
  output bob_one,
  output bob_two,
  output one_two,
  output ONE_2,
  output TWO_2,
  output bob_one_two_2,
  output bob_one_2,
  output bob_two_2,
  output one_two_2,
  output halt_2
);

  wire _7408_2_pin3, _7408_2_pin6, _7408_2_pin8, _7408_2_pin11, _7408_3_pin3, _7408_3_pin6, _7432_1_pin3,
       _7432_1_pin6, _7432_1_pin8, _7432_1_pin11, _7432_1_pin12, _7432_1_pin13, _7432_2_pin6, _7432_2_pin8,
       _7486_1_pin3, _7486_1_pin6, and_1_out, and_5_out, and_6_out, and_7_out, and_8_out, and_9_out,
       and_10_out, d_ff_1_q, nand_1_out, or_1_out, or_2_out, or_3_out, or_4_out, or_5_out, or_6_out,
       or_7_out, or_8_out, undriven, xor_1_out, xor_2_out, xor_3_out, xor_4_out;

  _7486 _7486_1 (
    .pin1(one_3), .pin2(1'b0), .pin3(_7486_1_pin3), .pin4(two_3), .pin5(1'b0), .pin6(_7486_1_pin6),
    .pin7(1'b0), .pin9(1'b1), .pin10(1'b1), .pin12(1'b1), .pin13(1'b1), .pin14(1'b1));  // open: pin8, pin11
  _7408 _7408_1 (
    .pin1(bob_3), .pin2(_7486_1_pin3), .pin3(bob_one_2), .pin4(bob_3), .pin5(_7486_1_pin6), .pin6(bob_two_2),
    .pin7(1'b0), .pin8(bob_one_two_2), .pin9(bob_two_2), .pin10(bob_one_2), .pin11(one_two_2),
    .pin12(_7486_1_pin6), .pin13(_7486_1_pin3), .pin14(1'b1));
  _7432 _7432_1 (
    .pin1(bob_one_2), .pin2(bob_two_2), .pin3(_7432_1_pin3), .pin4(one_two_2), .pin5(bob_one_two_2),
    .pin6(_7432_1_pin6), .pin7(1'b0), .pin8(_7432_1_pin8), .pin9(_7432_1_pin6), .pin10(_7432_1_pin3),
    .pin11(_7432_1_pin11), .pin12(_7432_1_pin12), .pin13(_7432_1_pin13), .pin14(1'b1));
  xor xor_1 (xor_1_out, d_ff_1_q, 1'b1);
  xor xor_2 (xor_2_out, one, undriven);
  xor xor_3 (xor_3_out, and_1_out, one);
  xor xor_4 (xor_4_out, and_1_out, two);
  _7408 _7408_2 (
    .pin1(rd_2), .pin2(wr_2), .pin3(_7408_2_pin3), .pin4(fw_2), .pin5(bk_2), .pin6(_7408_2_pin6),
    .pin7(1'b0), .pin8(_7408_2_pin8), .pin9(fw_2), .pin10(rd_2), .pin11(_7408_2_pin11), .pin12(bk_2),
    .pin13(rd_2), .pin14(1'b1));
  _7408 _7408_3 (
    .pin1(wr_2), .pin2(fw_2), .pin3(_7408_3_pin3), .pin4(wr_2), .pin5(bk_2), .pin6(_7408_3_pin6),
    .pin7(1'b0), .pin8(halt_2), .pin9(_7432_1_pin8), .pin10(_7432_1_pin11), .pin12(1'b1), .pin13(1'b1),
    .pin14(1'b1));  // open: pin11
  D_FF d_ff_1 (.D(xor_1_out), .C(swap), .Q(d_ff_1_q));  // open: nQ
  and and_1 (and_1_out, d_ff_1_q, xor_2_out);
  _7432 _7432_2 (
    .pin1(_7408_2_pin3), .pin2(_7408_2_pin6), .pin3(_7432_1_pin12), .pin4(_7408_2_pin11),
    .pin5(_7408_2_pin8), .pin6(_7432_2_pin6), .pin7(1'b0), .pin8(_7432_2_pin8), .pin9(_7408_3_pin3),
    .pin10(_7408_3_pin6), .pin11(_7432_1_pin13), .pin12(_7432_2_pin6), .pin13(_7432_2_pin8), .pin14(1'b1));
  and and_2 (bob_one, bob, xor_3_out);
  and and_3 (bob_two, bob, xor_4_out);
  and and_4 (one_two, xor_3_out, xor_4_out);
  and and_5 (and_5_out, rd, wr);
  and and_6 (and_6_out, fw, bk);
  and and_7 (and_7_out, rd, bk);
  and and_8 (and_8_out, rd, fw);
  and and_9 (and_9_out, wr, bk);
  and and_10 (and_10_out, wr, fw);
  and and_11 (bob_one_two, bob_one, bob_two);
  or or_1 (or_1_out, and_5_out, and_6_out);
  or or_2 (or_2_out, and_7_out, and_8_out);
  or or_3 (or_3_out, and_9_out, and_10_out);
  LED led_1 (.in(_7432_1_pin12));
  LED led_2 (.in(_7432_1_pin13));
  or or_4 (or_4_out, bob_one_two, bob_one);
  or or_5 (or_5_out, bob_two, one_two);
  or or_6 (or_6_out, or_2_out, or_3_out);
  or or_7 (or_7_out, or_4_out, or_5_out);
  or or_8 (or_8_out, or_1_out, or_6_out);
  and and_12 (BOB_2, bob, nand_1_out);
  and and_13 (ONE_2, xor_3_out, nand_1_out);
  and and_14 (TWO_2, xor_4_out, nand_1_out);
  nand nand_1 (nand_1_out, or_7_out, or_7_out);
  and and_15 (halt, nand_1_out, or_8_out);
endmodule
