// Digital circuit jelly-two-loop.dig as structural Verilog
module jelly_two_loop (
  input  zero,
  input  bob,
  input  one,
  input  rd,
  input  bob_2,
  input  one_2,
  input  wr,
  output A08,
  output A09
);

  wire and_1_out, and_2_out, and_3_out, and_4_out, and_5_out, and_6_out, not_1_out, xor_1_out, xor_2_out;

  and and_1 (and_1_out, bob, one);
  and and_2 (and_2_out, bob_2, one_2);
  and and_3 (and_3_out, and_1_out, rd);
  and and_4 (and_4_out, and_2_out, wr);
  not not_1 (not_1_out, zero);
  and and_5 (and_5_out, zero, and_3_out);
  and and_6 (and_6_out, not_1_out, and_4_out);
  xor xor_1 (xor_1_out, A08, 1'b1);
  xor xor_2 (xor_2_out, A09, 1'b1);
  D_FF d_ff_1 (.D(xor_1_out), .C(and_5_out), .Q(A08));  // open: nQ
  D_FF d_ff_2 (.D(xor_2_out), .C(and_6_out), .Q(A09));  // open: nQ

  // Notes on the sheet:
  //   Condition checks for [ and ] loops, 
  //   to change page of eeproms, 
  //   using address A08 and A09.
  //   lowercase names are internal, 
  //   before go to bus :)
  //   Toggle flip-flop logic,
  //   instant eeprom page change
endmodule
