// Digital circuit jelly-two-tape.dig as structural Verilog
module jelly_two_tape (
  input  [7:0] D0,
  input  D1,
  input  D2,
  input  D3,
  input  D4,
  input  D5,
  input  D6,
  input  D7,
  input  SERIN,
  input  CLR,
  input  SCLK,
  input  RCLK,
  input  OE,
  input  OEE,
  input  CEE,
  input  WEE,
  input  OES,
  input  CES,
  input  WES,
  output D0_2,
  output D1_2,
  output D2_2,
  output D3_2,
  output D4_2,
  output D5_2,
  output D6_2,
  output D7_2
);

  wire _74595_1_pin8, _74595_1_pin9, _74595_1_pin16;
  wire [15:0] _74595_1_pin2;

  _74595 _74595_1 (
    .pin1(_74595_1_pin2[14]), .pin2(_74595_1_pin2[13]), .pin3(_74595_1_pin2[12]), .pin4(_74595_1_pin2[11]),
    .pin5(_74595_1_pin2[10]), .pin6(_74595_1_pin2[9]), .pin7(_74595_1_pin2[8]), .pin8(_74595_1_pin8),
    .pin9(_74595_1_pin9), .pin10(CLR), .pin11(SCLK), .pin12(RCLK), .pin13(OE), .pin14(SERIN),
    .pin15(_74595_1_pin2[15]), .pin16(_74595_1_pin16));
  _74595 _74595_2 (
    .pin1(_74595_1_pin2[6]), .pin2(_74595_1_pin2[5]), .pin3(_74595_1_pin2[4]), .pin4(_74595_1_pin2[3]),
    .pin5(_74595_1_pin2[2]), .pin6(_74595_1_pin2[1]), .pin7(_74595_1_pin2[0]), .pin8(_74595_1_pin8),
    .pin10(CLR), .pin11(SCLK), .pin12(RCLK), .pin13(OE), .pin14(_74595_1_pin9), .pin15(_74595_1_pin2[7]),
    .pin16(_74595_1_pin16));  // open: pin9
  // _28c512 _28c512_1: pin names not known; wires that end beside it: _74595_1_pin2[15], _74595_1_pin2[12], _74595_1_pin2[7], _74595_1_pin2[6], _74595_1_pin2[5], _74595_1_pin2[4], _74595_1_pin2[3], _74595_1_pin2[2], _74595_1_pin2[1], _74595_1_pin2[0], D0[0], _74595_1_pin16, WEE, _74595_1_pin2[14], _74595_1_pin2[13], _74595_1_pin2[8], _74595_1_pin2[9], _74595_1_pin2[11], OEE, _74595_1_pin2[10]
  // A623308A a623308a_1: pin names not known; wires that end beside it: D0[1], D0[2], _74595_1_pin8, _74595_1_pin2[7], _74595_1_pin2[6], _74595_1_pin2[5], _74595_1_pin2[4], _74595_1_pin2[3], _74595_1_pin2[2], _74595_1_pin2[1], _74595_1_pin2[0], D0[0], D0[1], D0[2], _74595_1_pin8, _74595_1_pin16, WES, _74595_1_pin2[8], _74595_1_pin2[9], _74595_1_pin2[11], OES, _74595_1_pin2[10], CES, D0[7]
  LED led_1 (.in(D1));
  LED led_2 (.in(D0[0]));
  LED led_3 (.in(D3));
  LED led_4 (.in(D2));
  LED led_5 (.in(D5));
  LED led_6 (.in(D4));
  LED led_7 (.in(D7));
  LED led_8 (.in(D6));
  LED led_9 (.in(D0[1]));
  LED led_10 (.in(D0[0]));
  LED led_11 (.in(D0[3]));
  LED led_12 (.in(D0[2]));
  LED led_13 (.in(D0[5]));
  LED led_14 (.in(D0[4]));
  LED led_15 (.in(D0[7]));
  LED led_16 (.in(D0[6]));
  // Pins of 1 and 8 bits meet at D0

  assign D0_2 = D0[0];
  assign D1_2 = D0[1];
  assign D2_2 = D0[2];
  assign D3_2 = D0[3];
  assign D4_2 = D0[4];
  assign D5_2 = D0[5];
  assign D6_2 = D0[6];
  assign D7_2 = D0[7];
endmodule
