// Digital circuit jelly-two.dig as structural Verilog
module jelly_two (
  input  clock,
  input  halt,
  input  clear,
  input  [7:0] D0,
  input  D1,
  input  D2,
  input  D3,
  input  D4,
  input  D5,
  input  D6,
  input  D7,
  input  GND,
  input  in_29,
  input  HALT_2,
  input  CLOCK_2,
  input  in_32,
  input  in_33,
  input  VCC,
  input  in_35,
  output BOB,
  output ONE,
  output TWO,
  output RD,
  output WR,
  output FW,
  output BK,
  output HLT,
  output D0_2,
  output D1_2,
  output D2_2,
  output D3_2,
  output D4_2,
  output D5_2,
  output D6_2,
  output D7_2,
  output zero
);

  wire _2_pin1, _2_pin11, _28c16_2_p19, _28c16_2_p20, _28c16_2_p21, _28c16_4_p20, _7432_1_pin3, _7432_1_pin6,
       _7432_1_pin8, _7432_1_pin13, _7432_2_pin3, _7432_2_pin6, _74193_1_pin12, _74193_1_pin13,
       _74574_3_pin11, and_1_out, not_1_out;
  wire [2:0] _28c16_2_p11, _28c16_4_p9, _28c16_4_p21, _28c16_5_p9;
  wire [7:0] _28c16_1_p1, _28c16_2_p1, _28c16_3_p12, _74574_2_pin19;
  wire [7:3] _28c16_5_p20;

  not not_1 (not_1_out, halt);
  LED led_1 (.in(not_1_out));
  LED led_2 (.in(clock));
  LED led_3 (.in(clear));
  and and_1 (and_1_out, clock, not_1_out);
  // _28c16 _28c16_1: pin names not known; wires that end beside it: _28c16_1_p1[7], _28c16_1_p1[6], _28c16_1_p1[5], _28c16_1_p1[4], _28c16_1_p1[3], _28c16_1_p1[2], _28c16_1_p1[1], _28c16_1_p1[0], _28c16_2_p1[4], _28c16_2_p1[5], _28c16_2_p1[6], 1'b0, 1'b1, 1'b0, 1'b0, 1'b1, 1'b0, 1'b0, 1'b0
  _74193 _74193_1 (
    .pin1(1'b0), .pin2(_28c16_2_p1[1]), .pin3(_28c16_2_p1[0]), .pin4(1'b1), .pin5(and_1_out),
    .pin6(_28c16_2_p1[2]), .pin7(_28c16_2_p1[3]), .pin8(1'b0), .pin9(1'b0), .pin10(1'b0), .pin11(1'b1),
    .pin12(_74193_1_pin12), .pin13(_74193_1_pin13), .pin14(clear), .pin15(1'b0), .pin16(1'b1));
  LED led_4 (.in(_74193_1_pin13));
  LED led_5 (.in(_74193_1_pin12));
  // _28c16 _28c16_2: pin names not known; wires that end beside it: _28c16_2_p1[7], _28c16_2_p1[6], _28c16_2_p1[5], _28c16_2_p1[4], _28c16_2_p1[3], _28c16_2_p1[2], _28c16_2_p1[1], _28c16_2_p1[0], _28c16_2_p11[0], _28c16_2_p11[1], _28c16_2_p11[2], 1'b1, _28c16_2_p11[0], _28c16_2_p11[1], 1'b1, 1'b0, _28c16_2_p11[2], 1'b0, _28c16_2_p19, _28c16_2_p20, _28c16_2_p21
  // _28c16 _28c16_3: pin names not known; wires that end beside it: 1'b0, _28c16_2_p1[7], _28c16_2_p1[6], _28c16_2_p1[5], _28c16_2_p1[4], _28c16_2_p1[3], _28c16_2_p1[2], _28c16_2_p1[1], _28c16_2_p1[0], _28c16_3_p12[0], _28c16_3_p12[1], _28c16_3_p12[2], 1'b0, 1'b1, _28c16_2_p11[0], _28c16_2_p11[1], 1'b1, 1'b0, _28c16_2_p11[2], 1'b0, _28c16_3_p12[7], _28c16_3_p12[6], _28c16_3_p12[5]
  // _28c16 _28c16_4: pin names not known; wires that end beside it: _28c16_2_p1[7], _28c16_2_p1[6], _28c16_2_p1[5], _28c16_2_p1[4], _28c16_2_p1[3], _28c16_2_p1[2], _28c16_2_p1[1], _28c16_2_p1[0], _28c16_4_p9[0], _28c16_4_p9[1], _28c16_4_p9[2], 1'b0, 1'b1, _28c16_2_p11[0], _28c16_2_p11[1], 1'b1, 1'b0, _28c16_2_p11[2], 1'b0, _28c16_4_p20, _28c16_4_p21[2], _28c16_4_p21[1]
  _74574 _2 (
    .pin1(_2_pin1), .pin2(D0[0]), .pin3(D0[1]), .pin4(D0[2]), .pin5(CLOCK_2), .pin6(D0[4]), .pin7(D0[5]),
    .pin8(D0[6]), .pin9(D0[7]), .pin10(1'b0), .pin11(_2_pin11), .pin12(_28c16_1_p1[7]),
    .pin13(_28c16_1_p1[6]), .pin14(_28c16_1_p1[5]), .pin15(_28c16_1_p1[4]), .pin16(_28c16_1_p1[3]),
    .pin17(_28c16_1_p1[2]), .pin18(_28c16_1_p1[1]), .pin19(_28c16_1_p1[0]), .pin20(1'b1));
  _74574 _74574_1 (
    .pin1(_28c16_2_p20), .pin2(_28c16_3_p12[0]), .pin3(_28c16_3_p12[1]), .pin4(_28c16_3_p12[2]),
    .pin5(_28c16_3_p12[3]), .pin6(_28c16_3_p12[4]), .pin7(_28c16_3_p12[5]), .pin8(_28c16_3_p12[6]),
    .pin9(_28c16_3_p12[7]), .pin10(1'b0), .pin11(_28c16_2_p21), .pin12(D0[7]), .pin13(D0[6]), .pin14(D0[5]),
    .pin15(D0[4]), .pin16(CLOCK_2), .pin17(D0[2]), .pin18(D0[1]), .pin19(D0[0]), .pin20(1'b1));
  _74574 _74574_2 (
    .pin1(_28c16_4_p9[1]), .pin2(D0[0]), .pin3(D0[1]), .pin4(D0[2]), .pin5(CLOCK_2), .pin6(D0[4]),
    .pin7(D0[5]), .pin8(D0[6]), .pin9(D0[7]), .pin10(1'b0), .pin11(_28c16_4_p9[0]),
    .pin12(_74574_2_pin19[7]), .pin13(_74574_2_pin19[6]), .pin14(_74574_2_pin19[5]),
    .pin15(_74574_2_pin19[4]), .pin16(_74574_2_pin19[3]), .pin17(_74574_2_pin19[2]),
    .pin18(_74574_2_pin19[1]), .pin19(_74574_2_pin19[0]), .pin20(1'b1));
  // _28c16 _28c16_5: pin names not known; wires that end beside it: _74574_2_pin19[7], _74574_2_pin19[6], _74574_2_pin19[5], _74574_2_pin19[4], _74574_2_pin19[3], _74574_2_pin19[2], _74574_2_pin19[1], _74574_2_pin19[0], _28c16_5_p9[0], _28c16_5_p9[1], _28c16_5_p9[2], 1'b0, 1'b1, _28c16_4_p21[0], _28c16_4_p21[1], 1'b1, 1'b0, _28c16_4_p21[2], 1'b0, _28c16_5_p20[7], _28c16_5_p20[6], _28c16_5_p20[5]
  LED led_6 (.in(D0[0]));
  LED led_7 (.in(D0[0]));
  LED led_8 (.in(D0[2]));
  LED led_9 (.in(D0[1]));
  LED led_10 (.in(D2));
  LED led_11 (.in(D1));
  LED led_12 (.in(D0[4]));
  LED led_13 (.in(CLOCK_2));
  LED led_14 (.in(D4));
  LED led_15 (.in(D3));
  LED led_16 (.in(D0[6]));
  LED led_17 (.in(D0[5]));
  LED led_18 (.in(D6));
  LED led_19 (.in(D5));
  LED led_20 (.in(D0[7]));
  LED led_21 (.in(D7));
  _74574 _74574_3 (
    .pin1(_28c16_4_p9[2]), .pin2(_28c16_5_p9[0]), .pin3(_28c16_5_p9[1]), .pin4(_28c16_5_p9[2]),
    .pin5(_28c16_5_p20[3]), .pin6(_28c16_5_p20[4]), .pin7(_28c16_5_p20[5]), .pin8(_28c16_5_p20[6]),
    .pin9(_28c16_5_p20[7]), .pin10(1'b0), .pin11(_74574_3_pin11), .pin12(D0[7]), .pin13(D0[6]),
    .pin14(D0[5]), .pin15(D0[4]), .pin16(CLOCK_2), .pin17(D0[2]), .pin18(D0[1]), .pin19(D0[0]), .pin20(1'b1));
  LED led_22 (.in(D0[0]));
  LED led_23 (.in(D0[2]));
  LED led_24 (.in(D0[1]));
  LED led_25 (.in(D0[4]));
  LED led_26 (.in(CLOCK_2));
  LED led_27 (.in(D0[6]));
  LED led_28 (.in(D0[5]));
  LED led_29 (.in(D0[7]));
  _7432 _7432_1 (
    .pin1(_28c16_5_p9[0]), .pin2(_28c16_5_p9[1]), .pin3(_7432_1_pin3), .pin4(_28c16_5_p9[2]),
    .pin5(_28c16_5_p20[3]), .pin6(_7432_1_pin6), .pin7(1'b0), .pin8(_7432_1_pin8), .pin9(_7432_1_pin6),
    .pin10(_7432_1_pin3), .pin11(zero), .pin12(_7432_1_pin8), .pin13(_7432_1_pin13), .pin14(1'b1));
  _7432 _7432_2 (
    .pin1(_28c16_5_p20[4]), .pin2(_28c16_5_p20[5]), .pin3(_7432_2_pin3), .pin4(_28c16_5_p20[6]),
    .pin5(_28c16_5_p20[7]), .pin6(_7432_2_pin6), .pin7(1'b0), .pin8(_7432_1_pin13), .pin9(_7432_2_pin6),
    .pin10(_7432_2_pin3), .pin12(1'b1), .pin13(1'b1), .pin14(1'b1));  // open: pin11
  LED led_30 (.in(zero));
  // Pins of 1 and 8 bits meet at {D0[7:4], CLOCK_2, D0[2:0]}

  assign BK = D0[6];
  assign BOB = D0[0];
  assign D0[3] = CLOCK_2;
  assign D0_2 = D0[0];
  assign D1_2 = D0[1];
  assign D2_2 = D0[2];
  assign D3_2 = CLOCK_2;
  assign D4_2 = D0[4];
  assign D5_2 = D0[5];
  assign D6_2 = D0[6];
  assign D7_2 = D0[7];
  assign FW = D0[5];
  assign GND = D0[0];
  assign HALT_2 = D0[2];
  assign HLT = D0[7];
  assign in_29 = D0[1];
  assign in_32 = D0[4];
  assign in_33 = D0[5];
  assign in_35 = D0[7];
  assign ONE = D0[1];
  assign RD = CLOCK_2;
  assign TWO = D0[2];
  assign VCC = D0[6];
  assign WR = D0[4];
  // also tied to GND on the sheet: D0[0]
  // also tied to VCC on the sheet: D0[6]

  // Notes on the sheet:
  //   decoder eeprom
  //   pipeline counter
  //   FSM Bus
  //   math control eeprom
  //   code control eeprom
  //   tape control eeprom
  //   Self Bus
  //   lookup math eeprom
  //   Device Control
  //   Data Bus
  //   Extra Signals
  //   Zero detector
endmodule
