// Digital circuit 74flipflop.dig as structural Verilog
module _74flipflop (
  input  pre,
  input  clr,
  output out_3,
  output out_4
);

  wire nand_2_out;

  nand nand_1 (out_4, nand_2_out, clr);
  nand nand_2 (nand_2_out, out_4, pre);
  nand nand_3 (out_3, pre, out_4);
  nand nand_4 (out_4, out_3, clr);
endmodule
