// Digital circuit 74hc74-2-3-prg.dig as structural Verilog
module _74hc74_2_3_prg (
  input  in_7,
  input  in_8,
  input  in_9,
  output out_1,
  output out_2,
  output out_3,
  output out_4,
  output out_5,
  output out_6
);

  wire _7474_1_pin2, _7474_1_pin8, _7474_2_pin2, _7474_2_pin8, _7474_3_pin2, _7474_3_pin8;

  _7474 _7474_1 (
    .pin1(in_7), .pin2(_7474_1_pin2), .pin3(in_9), .pin4(in_8), .pin5(out_1), .pin6(_7474_1_pin2),
    .pin7(1'b0), .pin8(_7474_1_pin8), .pin9(out_2), .pin10(in_8), .pin11(out_1), .pin12(_7474_1_pin8),
    .pin13(in_7), .pin14(1'b1));
  _7474 _7474_2 (
    .pin1(in_7), .pin2(_7474_2_pin2), .pin3(out_2), .pin4(in_8), .pin5(out_3), .pin6(_7474_2_pin2),
    .pin7(1'b0), .pin8(_7474_2_pin8), .pin9(out_4), .pin10(in_8), .pin11(out_3), .pin12(_7474_2_pin8),
    .pin13(in_7), .pin14(1'b1));
  _7474 _7474_3 (
    .pin1(in_7), .pin2(_7474_3_pin2), .pin3(out_4), .pin4(in_8), .pin5(out_5), .pin6(_7474_3_pin2),
    .pin7(1'b0), .pin8(_7474_3_pin8), .pin9(out_6), .pin10(in_8), .pin11(out_5), .pin12(_7474_3_pin8),
    .pin13(in_7), .pin14(1'b1));
endmodule
