// Digital circuit base1.dig as structural Verilog
module base1 (
  input  Clock,
  input  in_2,
  input  Data_in,
  input  Carry_in,
  output Q_value,
  output Q_value_2,
  output Clock_2,
  output SEL,
  output SEL_2,
  output Carry_out
);

  wire nand_1_out, nand_2_out, nand_3_out, nand_4_out, nand_6_out, nand_8_out, nand_9_out, nand_10_out,
       nand_11_out, nand_12_out;

  nand nand_1 (nand_1_out, Carry_in, Q_value);
  nand nand_2 (nand_2_out, Carry_in, Q_value);
  nand nand_3 (nand_3_out, Carry_in, nand_1_out);
  nand nand_4 (nand_4_out, nand_1_out, Q_value);
  nand nand_5 (Carry_out, nand_2_out, nand_2_out);
  nand nand_6 (nand_6_out, nand_3_out, nand_4_out);
  nand nand_7 (SEL, in_2, in_2);
  nand nand_8 (nand_8_out, SEL, Data_in);
  nand nand_9 (nand_9_out, in_2, nand_6_out);
  nand nand_10 (nand_10_out, nand_8_out, nand_9_out);
  nand nand_11 (nand_11_out, nand_10_out, Clock);
  nand nand_12 (nand_12_out, nand_11_out, Clock);
  nand nand_13 (Q_value, nand_11_out, Q_value_2);
  nand nand_14 (Q_value_2, nand_12_out, Q_value);

  assign Clock_2 = Clock;
  assign SEL_2 = in_2;
endmodule
