// Digital circuit base2.dig as structural Verilog
module base2 (
);

  wire d_ff_1_q, d_ff_2_q, d_ff_3_q, d_ff_4_q, undriven, undriven_2;

  D_FF d_ff_1 (.D(undriven_2), .C(undriven), .Q(d_ff_1_q));  // open: nQ
  RAMDualPort ramdualport_1 ();  // open: A, Din, str, C, ld, D
  D_FF d_ff_2 (.D(d_ff_1_q), .C(undriven), .Q(d_ff_2_q));  // open: nQ
  D_FF d_ff_3 (.D(d_ff_2_q), .C(undriven), .Q(d_ff_3_q));  // open: nQ
  D_FF d_ff_4 (.D(d_ff_3_q), .C(undriven), .Q(d_ff_4_q));  // open: nQ
endmodule
