// Digital circuit base3.dig as structural Verilog
module base3 (
  input  in_4,
  input  in_5,
  input  in_6,
  input  in_7,
  input  in_11,
  input  in_12,
  input  in_13,
  output out_1,
  output out_2,
  output out_3,
  output out_8,
  output out_9,
  output out_10
);

  wire nand_1_out, nand_2_out, nand_3_out, nand_4_out, nand_7_out, nand_11_out, nand_12_out;

  nand nand_1 (nand_1_out, in_5, in_5);
  nand nand_2 (nand_2_out, in_4, in_4);
  nand nand_3 (nand_3_out, in_6, in_7);
  nand nand_4 (nand_4_out, nand_3_out, in_7);
  nand nand_5 (out_1, nand_1_out, in_4);
  nand nand_6 (out_2, in_5, nand_2_out);
  nand nand_7 (nand_7_out, in_13, in_13);
  nand nand_8 (out_3, out_1, out_2);
  nand nand_9 (out_8, nand_3_out, out_9);
  nand nand_10 (out_9, out_8, nand_4_out);
  nand nand_11 (nand_11_out, in_11, in_13);
  nand nand_12 (nand_12_out, in_12, nand_7_out);
  nand nand_13 (out_10, nand_11_out, nand_12_out);
endmodule
