// Digital circuit base6.dig as structural Verilog
module base6 (
  input  in_1,
  input  in_2,
  input  in_3,
  input  in_4,
  input  in_5,
  input  in_6,
  input  in_7,
  input  [7:0] in_8
);

  wire [7:0] add_1_s, driver_1_out, driver_2_out, register_1_q, register_2_q, register_3_q, register_4_q;

  Register #(.Bits(8)) register_1 (.D(driver_1_out), .C(in_7), .en(in_1), .Q(register_1_q));
  assign driver_1_out = in_3 ? register_3_q : 8'bz;  // Driver driver_1
  Register #(.Bits(8)) register_2 (.D(add_1_s), .C(in_7), .en(in_6), .Q(register_2_q));
  Register #(.Bits(8)) register_3 (.D(add_1_s), .C(in_7), .en(in_4), .Q(register_3_q));
  assign driver_2_out = in_2 ? register_1_q : 8'bz;  // Driver driver_2
  assign driver_2_out = in_5 ? register_2_q : 8'bz;  // Driver driver_3
  Register #(.Bits(8)) register_4 (.D(in_8), .C(in_7), .en(in_1), .Q(register_4_q));
  Add #(.Bits(8)) add_1 (.a(driver_2_out), .b(register_4_q), .c_i(in_7), .s(add_1_s));  // open: c_o
  // Pins of 1 and 8 bits meet at in_8
endmodule
