// Digital circuit check.dig as structural Verilog
module check (
  input  in_2,
  input  in_3,
  input  in_6,
  input  in_7,
  output out_1,
  output out_4,
  output out_5,
  output out_8
);

  wire nand_1_out, nand_2_out, nand_3_out, nand_4_out, nand_5_out;

  nand nand_1 (nand_1_out, in_2, in_3);
  nand nand_2 (nand_2_out, in_6, in_7);
  nand nand_3 (nand_3_out, in_2, nand_1_out);
  nand nand_4 (nand_4_out, in_3, nand_1_out);
  nand nand_5 (nand_5_out, nand_2_out, nand_2_out);
  nand nand_6 (out_1, nand_3_out, nand_3_out);
  nand nand_7 (out_4, nand_4_out, nand_4_out);
  nand nand_8 (out_5, in_6, nand_5_out);
  nand nand_9 (out_8, in_7, nand_5_out);
endmodule
