// Digital circuit chip-tape-diy.dig as structural Verilog
module chip_tape_diy (
  input  A0,
  input  A1,
  input  A2,
  input  A3,
  input  A4,
  input  A5,
  input  A6,
  input  A7,
  input  A8,
  input  A9,
  input  A10,
  input  A11,
  input  A12,
  input  A13,
  input  A14,
  input  A15,
  input  CLR,
  input  DN,
  input  UP,
  input  WE,
  input  OE,
  input  CS,
  input  LD,
  output D0,
  output D1,
  output D2,
  output D3,
  output D4,
  output D5,
  output D6,
  output D7
);

  wire _28c512_1_p1, _28c512_1_p2, _28c512_1_p3, _28c512_1_p4, _28c512_1_p5, _28c512_1_p6, _28c512_1_p7,
       _28c512_1_p8, _28c512_1_p9, _28c512_1_p10, _28c512_1_p14, _28c512_1_p15, _28c512_1_p17, _28c512_1_p18,
       _28c512_1_p19, _28c512_1_p20, _28c512_1_p21, _28c512_1_p23, _74193_1_pin12, _74193_1_pin13,
       _74193_2_pin12, _74193_2_pin13, _74193_3_pin12, _74193_3_pin13;

  // _28c512 _28c512_1: pin names not known; wires that end beside it: _28c512_1_p1, _28c512_1_p2, _28c512_1_p3, _28c512_1_p4, _28c512_1_p5, _28c512_1_p6, _28c512_1_p7, _28c512_1_p8, _28c512_1_p9, _28c512_1_p10, D0, D1, D2, _28c512_1_p14, _28c512_1_p15, WE, _28c512_1_p17, _28c512_1_p18, _28c512_1_p19, _28c512_1_p20, _28c512_1_p21, OE, _28c512_1_p23
  _74193 _74193_1 (
    .pin1(A1), .pin2(_28c512_1_p9), .pin3(_28c512_1_p10), .pin4(DN), .pin5(UP), .pin6(_28c512_1_p8),
    .pin7(_28c512_1_p7), .pin8(_28c512_1_p14), .pin9(A3), .pin10(A2), .pin11(LD), .pin12(_74193_1_pin12),
    .pin13(_74193_1_pin13), .pin14(CLR), .pin15(A0), .pin16(_28c512_1_p15));
  _74193 _74193_2 (
    .pin1(A5), .pin2(_28c512_1_p5), .pin3(_28c512_1_p6), .pin4(_74193_1_pin13), .pin5(_74193_1_pin12),
    .pin6(_28c512_1_p4), .pin7(_28c512_1_p3), .pin8(_28c512_1_p14), .pin9(A7), .pin10(A6), .pin11(LD),
    .pin12(_74193_2_pin12), .pin13(_74193_2_pin13), .pin14(CLR), .pin15(A4), .pin16(_28c512_1_p15));
  _74193 _74193_3 (
    .pin1(A9), .pin2(_28c512_1_p20), .pin3(_28c512_1_p19), .pin4(_74193_2_pin13), .pin5(_74193_2_pin12),
    .pin6(_28c512_1_p23), .pin7(_28c512_1_p21), .pin8(_28c512_1_p14), .pin9(A11), .pin10(A10), .pin11(LD),
    .pin12(_74193_3_pin12), .pin13(_74193_3_pin13), .pin14(CLR), .pin15(A8), .pin16(_28c512_1_p15));
  _74193 _74193_4 (
    .pin1(A13), .pin2(_28c512_1_p18), .pin3(_28c512_1_p2), .pin4(_74193_3_pin13), .pin5(_74193_3_pin12),
    .pin6(_28c512_1_p17), .pin7(_28c512_1_p1), .pin8(_28c512_1_p14), .pin9(A15), .pin10(A14), .pin11(LD),
    .pin14(CLR), .pin15(A12), .pin16(_28c512_1_p15));  // open: pin12, pin13
endmodule
