// Digital circuit counter-binary-both.dig as structural Verilog
module counter_binary_both (
  input  in_3,
  input  in_4,
  input  in_5,
  output out_1,
  output out_2,
  output out_6
);

  wire and_1_out, and_2_out, and_3_out, and_4_out, jk_ff_1_nq, jk_ff_2_nq, not_1_out, or_1_out, or_2_out;

  not not_1 (not_1_out, in_5);
  JK_FF jk_ff_1 (.J(in_4), .C(in_3), .K(in_4), .Q(out_6), .nQ(jk_ff_1_nq));
  and and_1 (and_1_out, in_5, out_6);
  and and_2 (and_2_out, jk_ff_1_nq, not_1_out);
  or or_1 (or_1_out, and_1_out, and_2_out);
  JK_FF jk_ff_2 (.J(or_1_out), .C(in_3), .K(or_1_out), .Q(out_1), .nQ(jk_ff_2_nq));
  and and_3 (and_3_out, and_1_out, out_1);
  and and_4 (and_4_out, jk_ff_2_nq, and_2_out);
  or or_2 (or_2_out, and_3_out, and_4_out);
  JK_FF jk_ff_3 (.J(or_2_out), .C(in_3), .K(or_2_out), .Q(out_2));  // open: nQ
endmodule
