// Digital circuit counter-binary-dn.dig as structural Verilog
module counter_binary_dn (
  input  in_4,
  input  in_5,
  output out_1,
  output out_2,
  output out_3
);

  wire and_1_out, jk_ff_1_nq, jk_ff_2_nq;

  JK_FF jk_ff_1 (.J(in_5), .C(in_4), .K(in_5), .Q(out_1), .nQ(jk_ff_1_nq));
  JK_FF jk_ff_2 (.J(jk_ff_1_nq), .C(in_4), .K(jk_ff_1_nq), .Q(out_2), .nQ(jk_ff_2_nq));
  and and_1 (and_1_out, jk_ff_1_nq, jk_ff_2_nq);
  JK_FF jk_ff_3 (.J(and_1_out), .C(in_4), .K(and_1_out), .Q(out_3));  // open: nQ
endmodule
