// Digital circuit counter-binary-up.dig as structural Verilog
module counter_binary_up (
  input  in_4,
  input  in_5,
  output out_1,
  output out_2,
  output out_3
);

  wire and_1_out;

  JK_FF jk_ff_1 (.J(in_5), .C(in_4), .K(in_5), .Q(out_1));  // open: nQ
  JK_FF jk_ff_2 (.J(out_1), .C(in_4), .K(out_1), .Q(out_2));  // open: nQ
  and and_1 (and_1_out, out_1, out_2);
  JK_FF jk_ff_3 (.J(and_1_out), .C(in_4), .K(and_1_out), .Q(out_3));  // open: nQ
endmodule
