// Digital circuit d-adder-4bits.dig as structural Verilog
module d_adder_4bits (
  input  A0,
  input  B0,
  input  A1,
  input  B1,
  input  A2,
  input  B2,
  input  A3,
  input  B3,
  input  carry_in,
  input  zero,
  input  sense,
  input  D0_D7,
  output S0,
  output S1,
  output S2,
  output S3,
  output carry_out,
  output B0_2,
  output B1_B7,
  output A0_A7
);

  wire nand_2_out, nand_3_out, nand_6_out, nand_7_out, nand_8_out, nand_9_out, nand_10_out, nand_11_out,
       nand_12_out, nand_13_out, nand_14_out, nand_15_out, nand_16_out, nand_17_out, nand_18_out,
       nand_19_out, nand_20_out, nand_21_out, nand_22_out, nand_23_out, nand_24_out, nand_25_out,
       nand_26_out, nand_27_out, nand_28_out, nand_29_out, nand_30_out, nand_31_out, nand_32_out,
       nand_33_out, nand_34_out, nand_35_out, nand_36_out, nand_37_out, nand_38_out, nand_39_out,
       nand_40_out, nand_41_out, nand_42_out, nand_43_out, nand_44_out;

  nand nand_1 (B0_2, zero, zero);
  nand nand_2 (nand_2_out, B0_2, sense);
  nand nand_3 (nand_3_out, B0_2, D0_D7);
  nand nand_4 (B1_B7, nand_2_out, nand_2_out);
  nand nand_5 (A0_A7, nand_3_out, nand_3_out);
  nand nand_6 (nand_6_out, A0, B0);
  nand nand_7 (nand_7_out, A1, B1);
  nand nand_8 (nand_8_out, A2, B2);
  nand nand_9 (nand_9_out, A3, B3);
  nand nand_10 (nand_10_out, A0, B0);
  nand nand_11 (nand_11_out, A1, B1);
  nand nand_12 (nand_12_out, A2, B2);
  nand nand_13 (nand_13_out, A3, B3);
  nand nand_14 (nand_14_out, A0, nand_10_out);
  nand nand_15 (nand_15_out, nand_10_out, B0);
  nand nand_16 (nand_16_out, A1, nand_11_out);
  nand nand_17 (nand_17_out, nand_11_out, B1);
  nand nand_18 (nand_18_out, A2, nand_12_out);
  nand nand_19 (nand_19_out, nand_12_out, B2);
  nand nand_20 (nand_20_out, A3, nand_13_out);
  nand nand_21 (nand_21_out, nand_13_out, B3);
  nand nand_22 (nand_22_out, nand_14_out, nand_15_out);
  nand nand_23 (nand_23_out, nand_16_out, nand_17_out);
  nand nand_24 (nand_24_out, nand_18_out, nand_19_out);
  nand nand_25 (nand_25_out, nand_20_out, nand_21_out);
  nand nand_26 (nand_26_out, nand_22_out, carry_in);
  nand nand_27 (nand_27_out, nand_22_out, carry_in);
  nand nand_28 (nand_28_out, nand_23_out, nand_36_out);
  nand nand_29 (nand_29_out, nand_23_out, nand_36_out);
  nand nand_30 (nand_30_out, nand_24_out, nand_39_out);
  nand nand_31 (nand_31_out, nand_24_out, nand_39_out);
  nand nand_32 (nand_32_out, nand_25_out, nand_42_out);
  nand nand_33 (nand_33_out, nand_25_out, nand_42_out);
  nand nand_34 (nand_34_out, nand_22_out, nand_26_out);
  nand nand_35 (nand_35_out, nand_26_out, carry_in);
  nand nand_36 (nand_36_out, nand_27_out, nand_6_out);
  nand nand_37 (nand_37_out, nand_23_out, nand_28_out);
  nand nand_38 (nand_38_out, nand_28_out, nand_36_out);
  nand nand_39 (nand_39_out, nand_29_out, nand_7_out);
  nand nand_40 (nand_40_out, nand_24_out, nand_30_out);
  nand nand_41 (nand_41_out, nand_30_out, nand_39_out);
  nand nand_42 (nand_42_out, nand_31_out, nand_8_out);
  nand nand_43 (nand_43_out, nand_25_out, nand_32_out);
  nand nand_44 (nand_44_out, nand_32_out, nand_42_out);
  nand nand_45 (carry_out, nand_33_out, nand_9_out);
  nand nand_46 (S0, nand_34_out, nand_35_out);
  nand nand_47 (S1, nand_37_out, nand_38_out);
  nand nand_48 (S2, nand_40_out, nand_41_out);
  nand nand_49 (S3, nand_43_out, nand_44_out);
endmodule
