// Digital circuit d-flip-flop-clear.dig as structural Verilog
module d_flip_flop_clear (
  input  in_3,
  input  in_4,
  input  in_5,
  output out_1,
  output out_2
);

  wire and_1_out, and_2_out, not_1_out, or_1_out;

  not not_1 (not_1_out, in_3);
  and and_1 (and_1_out, or_1_out, not_1_out);
  and and_2 (and_2_out, in_3, in_4);
  or or_1 (or_1_out, and_1_out, and_2_out);
  and and_3 (out_1, or_1_out, in_5);
  not not_2 (out_2, out_1);
endmodule
