// Digital circuit dff tests.dig as structural Verilog
module dff_tests (
  input  in_1,
  input  in_2,
  input  in_10,
  input  in_11,
  output out_3,
  output out_4,
  output out_5,
  output out_6,
  output out_7,
  output out_8,
  output out_9,
  output out_12,
  output out_13,
  output out_14,
  output out_15,
  output out_16
);

  wire and_1_out, and_2_out, and_3_out, and_4_out, and_5_out, and_6_out, and_7_out, and_8_out, d_ff_1_q,
       d_ff_2_q, d_ff_3_q, d_ff_4_q, nand_1_out, nand_2_out, nand_3_out, nand_4_out, nand_5_out, nand_6_out,
       nand_7_out, nand_8_out, nand_9_out, nand_11_out, nand_13_out, nand_15_out, nand_17_out, nand_18_out,
       nand_19_out, nand_20_out, nand_21_out, nand_22_out, nand_23_out, nand_24_out, nand_25_out,
       nand_26_out, nand_27_out, nand_28_out, not_1_out, or_1_out, or_2_out, or_3_out, or_4_out;

  not not_1 (not_1_out, in_2);
  D_FF d_ff_1 (.D(out_3), .C(in_1), .Q(d_ff_1_q), .nQ(out_3));
  and and_1 (and_1_out, not_1_out, out_3);
  and and_2 (and_2_out, in_2, d_ff_1_q);
  nand nand_1 (nand_1_out, out_12, in_11);
  nand nand_2 (nand_2_out, nand_1_out, in_11);
  nand nand_3 (nand_3_out, out_13, nand_26_out);
  nand nand_4 (nand_4_out, nand_3_out, nand_26_out);
  nand nand_5 (nand_5_out, out_14, nand_27_out);
  nand nand_6 (nand_6_out, nand_5_out, nand_27_out);
  nand nand_7 (nand_7_out, out_15, nand_28_out);
  nand nand_8 (nand_8_out, nand_7_out, nand_28_out);
  or or_1 (or_1_out, and_1_out, and_2_out);
  nand nand_9 (nand_9_out, nand_1_out, out_12);
  nand nand_10 (out_12, nand_9_out, nand_2_out);
  nand nand_11 (nand_11_out, nand_3_out, out_13);
  nand nand_12 (out_13, nand_11_out, nand_4_out);
  nand nand_13 (nand_13_out, nand_5_out, out_14);
  nand nand_14 (out_14, nand_13_out, nand_6_out);
  nand nand_15 (nand_15_out, nand_7_out, out_15);
  nand nand_16 (out_15, nand_15_out, nand_8_out);
  nand nand_17 (nand_17_out, in_10, in_10);
  D_FF d_ff_2 (.D(out_4), .C(or_1_out), .Q(d_ff_2_q), .nQ(out_4));
  nand nand_18 (nand_18_out, nand_17_out, nand_9_out);
  nand nand_19 (nand_19_out, in_10, out_12);
  nand nand_20 (nand_20_out, nand_17_out, nand_11_out);
  nand nand_21 (nand_21_out, in_10, out_13);
  nand nand_22 (nand_22_out, nand_17_out, nand_13_out);
  nand nand_23 (nand_23_out, in_10, out_14);
  nand nand_24 (nand_24_out, nand_17_out, nand_15_out);
  nand nand_25 (nand_25_out, in_10, out_15);
  and and_3 (and_3_out, not_1_out, out_4);
  and and_4 (and_4_out, in_2, d_ff_2_q);
  nand nand_26 (nand_26_out, nand_18_out, nand_19_out);
  nand nand_27 (nand_27_out, nand_20_out, nand_21_out);
  nand nand_28 (nand_28_out, nand_22_out, nand_23_out);
  nand nand_29 (out_16, nand_24_out, nand_25_out);
  or or_2 (or_2_out, and_3_out, and_4_out);
  D_FF d_ff_3 (.D(out_5), .C(or_2_out), .Q(d_ff_3_q), .nQ(out_5));
  and and_5 (and_5_out, not_1_out, out_5);
  and and_6 (and_6_out, in_2, d_ff_3_q);
  or or_3 (or_3_out, and_5_out, and_6_out);
  D_FF d_ff_4 (.D(out_6), .C(or_3_out), .Q(d_ff_4_q), .nQ(out_6));
  and and_7 (and_7_out, not_1_out, out_6);
  and and_8 (and_8_out, in_2, d_ff_4_q);
  or or_4 (or_4_out, and_7_out, and_8_out);

  assign out_7 = out_6;
  assign out_8 = out_5;
  assign out_9 = out_4;
endmodule
