// Digital circuit eeprom-tape-diy.dig as structural Verilog
module eeprom_tape_diy (
);

  wire _74193_1_pin2, _74193_1_pin3, _74193_1_pin6, _74193_1_pin7, _74193_1_pin8, _74193_1_pin12,
       _74193_1_pin13, _74193_1_pin14, _74193_1_pin16, _74193_2_pin2, _74193_2_pin3, _74193_2_pin6,
       _74193_2_pin7, _74193_2_pin12, _74193_2_pin13, _74193_3_pin2, _74193_3_pin3, _74193_3_pin6,
       _74193_3_pin7, _74193_3_pin12, _74193_3_pin13, _74193_4_pin2, _74193_4_pin3, _74193_4_pin6,
       _74193_4_pin7;

  // _28c512 _28c512_1: pin names not known
  _74193 _74193_1 (
    .pin2(_74193_1_pin2), .pin3(_74193_1_pin3), .pin6(_74193_1_pin6), .pin7(_74193_1_pin7),
    .pin8(_74193_1_pin8), .pin12(_74193_1_pin12), .pin13(_74193_1_pin13), .pin14(_74193_1_pin14),
    .pin16(_74193_1_pin16));  // open: pin1, pin4, pin5, pin9, pin10, pin11, pin15
  _74193 _74193_2 (
    .pin2(_74193_2_pin2), .pin3(_74193_2_pin3), .pin4(_74193_1_pin13), .pin5(_74193_1_pin12),
    .pin6(_74193_2_pin6), .pin7(_74193_2_pin7), .pin8(_74193_1_pin8), .pin12(_74193_2_pin12),
    .pin13(_74193_2_pin13), .pin14(_74193_1_pin14), .pin16(_74193_1_pin16));  // open: pin1, pin9, pin10, pin11, pin15
  _74193 _74193_3 (
    .pin2(_74193_3_pin2), .pin3(_74193_3_pin3), .pin4(_74193_2_pin13), .pin5(_74193_2_pin12),
    .pin6(_74193_3_pin6), .pin7(_74193_3_pin7), .pin8(_74193_1_pin8), .pin12(_74193_3_pin12),
    .pin13(_74193_3_pin13), .pin14(_74193_1_pin14), .pin16(_74193_1_pin16));  // open: pin1, pin9, pin10, pin11, pin15
  _74193 _74193_4 (
    .pin2(_74193_4_pin2), .pin3(_74193_4_pin3), .pin4(_74193_3_pin13), .pin5(_74193_3_pin12),
    .pin6(_74193_4_pin6), .pin7(_74193_4_pin7), .pin8(_74193_1_pin8), .pin14(_74193_1_pin14),
    .pin16(_74193_1_pin16));  // open: pin1, pin9, pin10, pin11, pin12, pin13, pin15
endmodule
