// Digital circuit jelly-two-bob.dig as structural Verilog
module jelly_two_bob (
  input  [7:0] in_1
);

  wire _28c512_1_p11, _28c512_1_p12, _28c512_1_p13, _28c512_1_p22, _7400_1_pin8, _7400_1_pin9, _7400_1_pin11,
       _7400_1_pin12, _7408_1_pin3, _74193_1_pin12, _74193_1_pin13, _74193_2_pin12, _74193_2_pin13,
       _74193_3_pin12, _74193_3_pin13;
  wire [7:0] _28c512_1_p19, _74193_1_pin3;

  _7400 _7400_1 (
    .pin1(1'b0), .pin2(1'b0), .pin4(1'b0), .pin5(1'b0), .pin7(1'b0), .pin8(_7400_1_pin8),
    .pin9(_7400_1_pin9), .pin10(_7400_1_pin9), .pin11(_7400_1_pin11), .pin12(_7400_1_pin12),
    .pin13(_7400_1_pin12), .pin14(1'b1));  // open: pin3, pin6
  PullUp pullup_1 (.out(_7400_1_pin11));
  PullUp pullup_2 (.out(_7400_1_pin8));
  _74193 _74193_1 (
    .pin1(1'b0), .pin2(_74193_1_pin3[1]), .pin3(_74193_1_pin3[0]), .pin4(_7400_1_pin8), .pin5(_7400_1_pin11),
    .pin6(_74193_1_pin3[2]), .pin7(_74193_1_pin3[3]), .pin8(1'b0), .pin9(1'b0), .pin10(1'b0), .pin11(1'b1),
    .pin12(_74193_1_pin12), .pin13(_74193_1_pin13), .pin14(in_1[7]), .pin15(1'b0), .pin16(1'b1));
  _74193 _74193_2 (
    .pin1(1'b0), .pin2(_74193_1_pin3[5]), .pin3(_74193_1_pin3[4]), .pin4(_74193_1_pin13),
    .pin5(_74193_1_pin12), .pin6(_74193_1_pin3[6]), .pin7(_74193_1_pin3[7]), .pin8(1'b0), .pin9(1'b0),
    .pin10(1'b0), .pin11(1'b1), .pin12(_74193_2_pin12), .pin13(_74193_2_pin13), .pin14(in_1[7]),
    .pin15(1'b0), .pin16(1'b1));
  // _28c512 _28c512_1: pin names not known; wires that end beside it: _28c512_1_p19[7], _28c512_1_p19[4], _74193_1_pin3[0], _74193_1_pin3[1], _74193_1_pin3[2], _74193_1_pin3[3], _74193_1_pin3[4], _74193_1_pin3[5], _74193_1_pin3[6], _74193_1_pin3[7], _28c512_1_p11, _28c512_1_p12, _28c512_1_p13, 1'b0, 1'b1, 1'b1, _28c512_1_p19[6], _28c512_1_p19[5], _28c512_1_p19[0], _28c512_1_p19[1], _28c512_1_p19[3], _28c512_1_p22, _28c512_1_p19[2]
  _74193 _74193_3 (
    .pin1(1'b0), .pin2(_28c512_1_p19[1]), .pin3(_28c512_1_p19[0]), .pin4(_74193_2_pin13),
    .pin5(_74193_2_pin12), .pin6(_28c512_1_p19[2]), .pin7(_28c512_1_p19[3]), .pin8(1'b0), .pin9(1'b0),
    .pin10(1'b0), .pin11(1'b1), .pin12(_74193_3_pin12), .pin13(_74193_3_pin13), .pin14(in_1[7]),
    .pin15(1'b0), .pin16(1'b1));
  _74193 _74193_4 (
    .pin1(1'b0), .pin2(_28c512_1_p19[5]), .pin3(_28c512_1_p19[4]), .pin4(_74193_3_pin13),
    .pin5(_74193_3_pin12), .pin6(_28c512_1_p19[6]), .pin7(_28c512_1_p19[7]), .pin8(1'b0), .pin9(1'b0),
    .pin10(1'b0), .pin11(1'b1), .pin14(in_1[7]), .pin15(1'b0), .pin16(1'b1));  // open: pin12, pin13
  _7408 _7408_1 (
    .pin1(in_1[2]), .pin2(in_1[3]), .pin3(_7408_1_pin3), .pin4(in_1[2]), .pin5(in_1[4]),
    .pin6(_28c512_1_p22), .pin7(1'b0), .pin8(_7400_1_pin12), .pin9(in_1[2]), .pin10(in_1[5]),
    .pin11(_7400_1_pin9), .pin12(in_1[2]), .pin13(in_1[6]), .pin14(1'b1));
  LED led_1 (.in(_7400_1_pin12));
  LED led_2 (.in(_7400_1_pin9));
  LED led_3 (.in(_28c512_1_p22));
  LED led_4 (.in(_7408_1_pin3));
  LED led_5 (.in(in_1[2]));

  // Notes on the sheet:
  //   BOB
  //   RD
  //   WR
  //   FW
  //   BK
  //   RST
endmodule
