// Digital circuit jelly-two-ctrl.dig as structural Verilog
module jelly_two_ctrl (
  input  [7:0] in_1
);

  wire _7408_1_pin2, _7408_1_pin3, _7408_1_pin5, _7408_1_pin6, _7408_1_pin8, _7408_1_pin10, _7408_1_pin11,
       _7408_1_pin13, _7408_2_pin1, _7408_2_pin9;

  LED led_1 (.in(_7408_1_pin3));
  LED led_2 (.in(_7408_1_pin6));
  LED led_3 (.in(_7408_1_pin8));
  LED led_4 (.in(_7408_1_pin11));
  _7408 _7408_1 (
    .pin1(in_1[2]), .pin2(_7408_1_pin2), .pin3(_7408_1_pin3), .pin4(in_1[2]), .pin5(_7408_1_pin5),
    .pin6(_7408_1_pin6), .pin7(1'b0), .pin8(_7408_1_pin8), .pin9(in_1[2]), .pin10(_7408_1_pin10),
    .pin11(_7408_1_pin11), .pin12(in_1[2]), .pin13(_7408_1_pin13), .pin14(1'b1));
  _7408 _7408_2 (
    .pin1(_7408_2_pin1), .pin2(in_1[4]), .pin3(_7408_1_pin2), .pin4(_7408_2_pin1), .pin5(in_1[3]),
    .pin6(_7408_1_pin5), .pin7(1'b0), .pin8(_7408_1_pin10), .pin9(_7408_2_pin9), .pin10(in_1[6]),
    .pin11(_7408_1_pin13), .pin12(_7408_2_pin9), .pin13(in_1[5]), .pin14(1'b1));
  _7400 _7400_1 (
    .pin1(in_1[4]), .pin2(in_1[3]), .pin3(_7408_2_pin1), .pin4(1'b0), .pin5(1'b0), .pin7(1'b0), .pin9(1'b0),
    .pin10(1'b0), .pin11(_7408_2_pin9), .pin12(in_1[6]), .pin13(in_1[5]), .pin14(1'b1));  // open: pin6, pin8
  LED led_5 (.in(in_1[6]));
  LED led_6 (.in(in_1[5]));
  LED led_7 (.in(in_1[4]));
  LED led_8 (.in(in_1[3]));
  LED led_9 (.in(in_1[2]));

  // Notes on the sheet:
  //   ONE
  //   TWO
  //   BOB
  //   RD
  //   WR
  //   FW
  //   BK
  //   RST
endmodule
