// Digital circuit nand-d-flip-flop.dig as structural Verilog
module nand_d_flip_flop (
  input  in_3,
  input  in_4,
  input  in_5,
  output out_1,
  output out_2
);

  wire nand_1_out, nand_2_out, nand_3_out;

  nand nand_1 (nand_1_out, in_4, in_3);
  nand nand_2 (nand_2_out, nand_1_out, in_5);
  nand nand_3 (nand_3_out, nand_2_out, in_5);
  nand nand_4 (out_2, nand_2_out, out_1);
  nand nand_5 (out_1, out_2, nand_3_out);
endmodule
