// Digital circuit swap-active.dig as structural Verilog
module swap_active (
  input  always_1,
  input  one,
  input  two,
  input  swap_2,
  output SWAP,
  output TWO_2,
  output ONE_2
);

  wire nand_1_out, xor_1_out, xor_2_out, xor_3_out;

  xor xor_1 (xor_1_out, SWAP, always_1);
  xor xor_2 (xor_2_out, SWAP, one);
  xor xor_3 (xor_3_out, SWAP, two);
  D_FF d_ff_1 (.D(xor_1_out), .C(swap_2), .Q(SWAP));  // open: nQ
  nand nand_1 (nand_1_out, xor_3_out, xor_2_out);
  and and_1 (ONE_2, xor_2_out, nand_1_out);
  and and_2 (TWO_2, xor_3_out, nand_1_out);
endmodule
