// Digital circuit toggle or last.dig as structural Verilog
module toggle_or_last (
  input  in_3,
  input  in_4,
  input  in_7,
  input  in_8,
  input  in_9,
  input  in_10,
  output out_1,
  output out_2,
  output out_5,
  output out_6,
  output out_11,
  output out_12
);

  wire and_1_out, and_2_out, and_3_out, and_4_out, and_5_out, and_6_out, nand_1_out, nand_2_out, nand_3_out,
       nand_4_out, nand_5_out, nand_6_out, or_1_out, or_2_out, undriven, undriven_2, undriven_3, undriven_4,
       undriven_5, undriven_6, undriven_7, undriven_8, undriven_9, undriven_10, undriven_11, undriven_12;

  nand nand_1 (nand_1_out, in_3, in_4);
  D_FF d_ff_1 (.D(in_3), .C(nand_1_out), .Q(out_1));  // open: nQ
  D_FF d_ff_2 (.D(in_4), .C(nand_1_out), .Q(out_2));  // open: nQ
  D_FF d_ff_3 (.D(in_7), .C(in_8), .Q(out_5));  // open: nQ
  D_FF d_ff_4 (.D(in_8), .C(in_7), .Q(out_6));  // open: nQ
  nand nand_2 (nand_2_out, undriven_3, undriven_3);
  nand nand_3 (nand_3_out, undriven_4, undriven_4);
  or or_1 (or_1_out, undriven, undriven_2);
  and and_1 (and_1_out, undriven_9, undriven_8);
  and and_2 (and_2_out, undriven_6, undriven_7);
  nand nand_4 (nand_4_out, undriven_11, undriven_11);
  and and_3 (and_3_out, nand_2_out, nand_3_out);
  or or_2 (or_2_out, or_1_out, undriven_10);
  nand nand_5 (nand_5_out, in_9, in_10);
  and and_4 (and_4_out, and_1_out, undriven_5);
  and and_5 (and_5_out, and_2_out, nand_4_out);
  and and_6 (and_6_out, and_3_out, undriven_12);
  nand nand_6 (nand_6_out, or_2_out, or_2_out);
  JK_FF jk_ff_1 (.J(in_9), .C(nand_5_out), .K(nand_5_out), .Q(out_11));  // open: nQ
  JK_FF jk_ff_2 (.J(in_10), .C(nand_5_out), .K(nand_5_out), .Q(out_12));  // open: nQ
endmodule
