// Digital circuit usefulls.dig as structural Verilog
module usefulls (
  input  in_3,
  input  in_4,
  input  in_6,
  input  in_7,
  input  in_8,
  input  in_9,
  input  in_10,
  input  in_15,
  input  in_16,
  input  in_21,
  output out_1,
  output out_2,
  output out_5,
  output out_11,
  output out_12,
  output out_13,
  output out_14,
  output out_17,
  output out_18,
  output out_19,
  output out_20,
  output out_22,
  output out_23,
  output out_24,
  output out_25
);

  wire nand_1_out, nand_2_out, nand_3_out, nand_4_out, nand_5_out, nand_6_out, nand_7_out, nand_8_out,
       nand_9_out, nand_10_out, nand_11_out, nand_19_out, nand_20_out, nand_21_out, nand_22_out, nand_23_out,
       nand_24_out, nand_25_out, nand_26_out, nand_27_out, nand_28_out, nand_29_out;

  nand nand_1 (nand_1_out, in_9, in_9);
  nand nand_2 (nand_2_out, in_10, in_10);
  nand nand_3 (nand_3_out, in_6, in_6);
  nand nand_4 (nand_4_out, in_3, in_4);
  nand nand_5 (nand_5_out, nand_4_out, in_4);
  nand nand_6 (nand_6_out, in_9, in_10);
  nand nand_7 (nand_7_out, in_9, nand_2_out);
  nand nand_8 (nand_8_out, nand_1_out, in_10);
  nand nand_9 (nand_9_out, nand_1_out, nand_2_out);
  nand nand_10 (nand_10_out, in_7, in_6);
  nand nand_11 (nand_11_out, in_8, nand_3_out);
  nand nand_12 (out_1, nand_4_out, out_2);
  nand nand_13 (out_2, out_1, nand_5_out);
  nand nand_14 (out_11, nand_6_out, nand_6_out);
  nand nand_15 (out_12, nand_7_out, nand_7_out);
  nand nand_16 (out_13, nand_8_out, nand_8_out);
  nand nand_17 (out_14, nand_9_out, nand_9_out);
  nand nand_18 (out_5, nand_10_out, nand_11_out);
  nand nand_19 (nand_19_out, in_21, in_21);
  nand nand_20 (nand_20_out, in_15, in_15);
  nand nand_21 (nand_21_out, in_16, in_16);
  nand nand_22 (nand_22_out, in_15, in_16);
  nand nand_23 (nand_23_out, in_15, nand_21_out);
  nand nand_24 (nand_24_out, nand_20_out, in_16);
  nand nand_25 (nand_25_out, nand_20_out, nand_21_out);
  nand nand_26 (nand_26_out, in_21, in_15);
  nand nand_27 (nand_27_out, in_21, nand_19_out);
  nand nand_28 (nand_28_out, in_15, nand_20_out);
  nand nand_29 (nand_29_out, nand_20_out, nand_19_out);
  nand nand_30 (out_17, nand_22_out, nand_22_out);
  nand nand_31 (out_18, nand_23_out, nand_23_out);
  nand nand_32 (out_19, nand_24_out, nand_24_out);
  nand nand_33 (out_20, nand_25_out, nand_25_out);
  nand nand_34 (out_22, nand_26_out, nand_26_out);
  nand nand_35 (out_23, nand_27_out, nand_27_out);
  nand nand_36 (out_24, nand_28_out, nand_28_out);
  nand nand_37 (out_25, nand_29_out, nand_29_out);
endmodule
