// Digital circuit eeprom-page-select.dig as structural Verilog
module eeprom_page_select (
  input  D7,
  input  D6,
  input  D5,
  input  D4,
  input  in_8,
  input  in_9,
  input  in_10,
  input  D7_2,
  input  D6_2,
  input  D5_2,
  input  D4_2,
  input  K2,
  input  K1,
  input  k0,
  output A10,
  output A9,
  output A8,
  output out_11,
  output A10_2,
  output A9_2,
  output A8_2,
  output NOT_OPCODE
);

  wire nand_1_out, nand_2_out, nand_3_out, nand_4_out, nand_5_out, nand_6_out, nand_7_out, nand_8_out,
       nand_9_out, nand_10_out, nand_11_out, nand_12_out, or_1_out, or_2_out, or_3_out, or_4_out, or_5_out,
       or_7_out, or_8_out, or_9_out;

  nand nand_1 (nand_1_out, D7, D7);
  nand nand_2 (nand_2_out, D6, D6);
  nand nand_3 (nand_3_out, D5, D5);
  nand nand_4 (nand_4_out, D4, D4);
  nand nand_5 (nand_5_out, nand_1_out, nand_2_out);
  nand nand_6 (nand_6_out, nand_3_out, nand_4_out);
  or or_1 (or_1_out, D7_2, D6_2);
  or or_2 (or_2_out, D5_2, D4_2);
  or or_3 (or_3_out, K2, K2);
  or or_4 (or_4_out, K1, K1);
  or or_5 (or_5_out, k0, k0);
  nand nand_7 (nand_7_out, nand_5_out, nand_5_out);
  nand nand_8 (nand_8_out, nand_6_out, nand_6_out);
  or or_6 (NOT_OPCODE, or_1_out, or_2_out);
  or or_7 (or_7_out, or_3_out, or_3_out);
  or or_8 (or_8_out, or_4_out, or_4_out);
  or or_9 (or_9_out, or_5_out, or_5_out);
  nand nand_9 (nand_9_out, nand_7_out, nand_8_out);
  nand nand_10 (nand_10_out, in_8, in_8);
  nand nand_11 (nand_11_out, in_9, in_9);
  nand nand_12 (nand_12_out, in_10, in_10);
  or or_10 (A10_2, NOT_OPCODE, or_7_out);
  or or_11 (A9_2, NOT_OPCODE, or_8_out);
  or or_12 (A8_2, NOT_OPCODE, or_9_out);
  nand nand_13 (out_11, nand_9_out, nand_9_out);
  nand nand_14 (A10, out_11, nand_10_out);
  nand nand_15 (A9, out_11, nand_11_out);
  nand nand_16 (A8, out_11, nand_12_out);

  // Notes on the sheet:
  //   those are for eeprom upper bits,
  //   k0, k1, k2 with same delay as 
  //   D4, D5, D6, D7 to map a page
  //   for non opcodes
endmodule
